// Logisim project 1901cs75_TermProject.circ as structural Verilog: 8 circuits, main circuit Main Circuit
module ALU (
  input  [7:0] A,
  input  [7:0] B,
  input  [3:0] Sel,
  output [7:0] Out
);

  wire [7:0] adder_1_out, and_1_out, or_1_out, subtractor_1_out, xor_1_out;

  Adder adder_1 (.a(A), .b(B), .out(adder_1_out));  // open: cin, cout
  Subtractor subtractor_1 (.a(A), .b(B), .out(subtractor_1_out));  // open: bin, bout
  assign and_1_out = A & B;  // AND_Gate and_1, 8 bits wide
  assign or_1_out = A | B;  // OR_Gate or_1, 8 bits wide
  assign xor_1_out = A ^ B;  // XOR_Gate xor_1, 8 bits wide
  Multiplexer #(.select(4), .width(8)) multiplexer_1 (
    .in0(adder_1_out), .in1(subtractor_1_out), .in2(and_1_out), .in4(or_1_out), .in8(xor_1_out), .out(Out),
    .sel(Sel));  // open: in3, in5, in6, in7, in9, in10, in11, in12, in13, in14, in15, en
endmodule

module RF (
  input  [7:0] WD,
  input  [1:0] RA1,
  input  [1:0] RA2,
  input  [1:0] wa,
  input  Clock,
  input  RW,
  output [7:0] A,
  output [7:0] A_2,
  output [7:0] A_3,
  output [7:0] A_4,
  output [7:0] R1,
  output [7:0] R2
);

  wire and_1_out, and_2_out, and_3_out, and_4_out, decoder_1_out0, decoder_1_out1, decoder_1_out2,
       decoder_1_out3;

  Decoder #(.select(2)) decoder_1 (
    .out0(decoder_1_out0), .out1(decoder_1_out1), .out2(decoder_1_out2), .out3(decoder_1_out3), .sel(wa));  // open: en
  and and_1 (and_1_out, decoder_1_out0, RW);
  and and_2 (and_2_out, decoder_1_out1, RW);
  and and_3 (and_3_out, decoder_1_out2, RW);
  and and_4 (and_4_out, decoder_1_out3, RW);
  Register #(.trigger("falling")) register_1 (.D(WD), .en(and_1_out), .Q(A), .clk(Clock));  // open: clr
  Register #(.trigger("falling")) register_2 (.D(WD), .en(and_2_out), .Q(A_2), .clk(Clock));  // open: clr
  Register #(.trigger("falling")) register_3 (.D(WD), .en(and_3_out), .Q(A_3), .clk(Clock));  // open: clr
  Register #(.trigger("falling")) register_4 (.D(WD), .en(and_4_out), .Q(A_4), .clk(Clock));  // open: clr
  Multiplexer #(.select(2), .width(8)) multiplexer_1 (
    .in0(A), .in1(A_2), .in2(A_3), .in3(A_4), .out(R1), .sel(RA1));  // open: en
  Multiplexer #(.select(2), .width(8)) multiplexer_2 (
    .in0(A), .in1(A_2), .in2(A_3), .in3(A_4), .out(R2), .sel(RA2));  // open: en
endmodule

module Main_Circuit (
  input  ResetPC,
  output [7:0] A,
  output [7:0] A_2,
  output [7:0] A_3,
  output [7:0] A_4
);

  wire CLK, controller_1_alusel, controller_1_asel, controller_1_msw, controller_1_wasel, controller_1_wbsel,
       controller_1_wsel, exdmr_1_ms_2, exdmr_1_rw_2, exdmr_1_wb_2, id_ex_register_1_alu_sel_2,
       id_ex_register_1_asel_2, id_ex_register_1_ms_2, id_ex_register_1_rw_2, id_ex_register_1_wb_2,
       multiplexer_2_out, multiplexer_3_out, multiplexer_5_out, multiplexer_7_out, multiplexer_8_out,
       register_3_q, register_4_q, staller_1_bubble, staller_1_if_idw, staller_1_pcw;
  wire [1:0] EXDMRD, id_ex_register_1_wba_2, inst_decoder_1_rd, inst_decoder_1_rs, inst_decoder_1_rt,
       multiplexer_1_out, multiplexer_4_out, register_5_q;
  wire [3:0] controller_1_alufun, id_ex_register_1_ialu_2, id_ex_register_1_ralu_2, inst_decoder_1_fun,
       multiplexer_9_out, multiplexer_11_out;
  wire [5:0] inst_decoder_1_immediate, inst_decoder_1_op;
  wire [7:0] adder_1_out, alu_1_out, bit_extender_1_out, exdmr_1_a_2, exdmr_1_alures_2, exdmr_1_d_2,
       id_ex_register_1_a_2, id_ex_register_1_b_2, id_ex_register_1_imm_2, id_ex_register_1_msadd_2,
       inst_decoder_1_address, multiplexer_6_out, multiplexer_10_out, multiplexer_12_out, ram_2_data,
       register_1_q, register_6_q, register_7_q, rf_1_r1, rf_1_r2;
  wire [15:0] ram_1_data, register_2_q;

  Clock u_Clk (.out(CLK));
  Register register_1 (.D(adder_1_out), .en(staller_1_pcw), .Q(register_1_q), .clk(CLK), .clr(ResetPC));
  Adder adder_1 (.a(8'h1), .b(register_1_q), .out(adder_1_out));  // open: cin, cout
  RAM #(.dataWidth(16)) ram_1 (.addr(register_1_q), .data(ram_1_data), .clk(CLK), .ld(1'b1));  // open: sel, clr
  Register #(.width(16)) register_2 (.D(ram_1_data), .en(staller_1_if_idw), .Q(register_2_q), .clk(CLK));  // open: clr
  Staller staller_1 (
    .ID_EX_RW(id_ex_register_1_rw_2), .ID_EX_rd(id_ex_register_1_wba_2), .EX_DM_rd(EXDMRD),
    .EX_DM_RW(exdmr_1_rw_2), .Instruction_Next(register_2_q), .PCw(staller_1_pcw), .IF_IDw(staller_1_if_idw),
    .Bubble(staller_1_bubble));
  Inst_Decoder inst_decoder_1 (
    .Instruction(register_2_q), .OP(inst_decoder_1_op), .RS(inst_decoder_1_rs), .RT(inst_decoder_1_rt),
    .RD(inst_decoder_1_rd), .Fun(inst_decoder_1_fun), .Immediate(inst_decoder_1_immediate),
    .Address(inst_decoder_1_address));
  Multiplexer #(.width(2)) multiplexer_1 (
    .in0(inst_decoder_1_rd), .in1(inst_decoder_1_rs), .out(multiplexer_1_out), .sel(controller_1_wasel));  // open: en
  Controller controller_1 (
    .OP_Code(inst_decoder_1_op), .WSel(controller_1_wsel), .WBSel(controller_1_wbsel),
    .Msw(controller_1_msw), .ASel(controller_1_asel), .ALUSel(controller_1_alusel),
    .ALUFun(controller_1_alufun), .waSel(controller_1_wasel));
  assign bit_extender_1_out = {{2{inst_decoder_1_immediate[5]}}, inst_decoder_1_immediate};  // Bit_Extender bit_extender_1
  Multiplexer multiplexer_2 (
    .in0(controller_1_wsel), .in1(1'b0), .out(multiplexer_2_out), .sel(staller_1_bubble));  // open: en
  Multiplexer multiplexer_3 (
    .in0(controller_1_wbsel), .in1(1'b0), .out(multiplexer_3_out), .sel(staller_1_bubble));  // open: en
  Multiplexer #(.width(2)) multiplexer_4 (
    .in0(multiplexer_1_out), .in1(2'b00), .out(multiplexer_4_out), .sel(staller_1_bubble));  // open: en
  Multiplexer multiplexer_5 (
    .in0(controller_1_msw), .in1(1'b0), .out(multiplexer_5_out), .sel(staller_1_bubble));  // open: en
  Multiplexer #(.width(8)) multiplexer_6 (
    .in0(inst_decoder_1_address), .in1({8{1'b0}}), .out(multiplexer_6_out), .sel(staller_1_bubble));  // open: en
  Multiplexer multiplexer_7 (
    .in0(controller_1_asel), .in1(1'b0), .out(multiplexer_7_out), .sel(staller_1_bubble));  // open: en
  Multiplexer multiplexer_8 (
    .in0(controller_1_alusel), .in1(1'b0), .out(multiplexer_8_out), .sel(staller_1_bubble));  // open: en
  Multiplexer #(.width(4)) multiplexer_9 (
    .in0(controller_1_alufun), .in1(4'b0000), .out(multiplexer_9_out), .sel(staller_1_bubble));  // open: en
  RF rf_1 (
    .WD(multiplexer_12_out), .RA1(inst_decoder_1_rs), .RA2(inst_decoder_1_rt), .wa(register_5_q),
    .Clock(CLK), .A(A), .A_2(A_2), .A_3(A_3), .A_4(A_4), .RW(register_3_q), .R1(rf_1_r1), .R2(rf_1_r2));
  ID_EX_Register id_ex_register_1 (
    .CLK(CLK), .RW(multiplexer_2_out), .WB(multiplexer_3_out), .WBA(multiplexer_4_out),
    .MS(multiplexer_5_out), .MSADD(multiplexer_6_out), .ASEL(multiplexer_7_out), .ALU_SEL(multiplexer_8_out),
    .IALU(multiplexer_9_out), .A(rf_1_r1), .B(rf_1_r2), .IMM(bit_extender_1_out), .RALU(inst_decoder_1_fun),
    .RW_2(id_ex_register_1_rw_2), .WB_2(id_ex_register_1_wb_2), .WBA_2(id_ex_register_1_wba_2),
    .MS_2(id_ex_register_1_ms_2), .MSADD_2(id_ex_register_1_msadd_2), .ASEL_2(id_ex_register_1_asel_2),
    .ALU_SEL_2(id_ex_register_1_alu_sel_2), .IALU_2(id_ex_register_1_ialu_2), .A_2(id_ex_register_1_a_2),
    .B_2(id_ex_register_1_b_2), .IMM_2(id_ex_register_1_imm_2), .RALU_2(id_ex_register_1_ralu_2));
  Multiplexer #(.width(8)) multiplexer_10 (
    .in0(id_ex_register_1_a_2), .in1(id_ex_register_1_imm_2), .out(multiplexer_10_out),
    .sel(id_ex_register_1_asel_2));  // open: en
  ALU alu_1 (.A(multiplexer_10_out), .B(id_ex_register_1_b_2), .Sel(multiplexer_11_out), .Out(alu_1_out));
  Multiplexer #(.width(4)) multiplexer_11 (
    .in0(id_ex_register_1_ralu_2), .in1(id_ex_register_1_ialu_2), .out(multiplexer_11_out),
    .sel(id_ex_register_1_alu_sel_2));  // open: en
  EXDMR exdmr_1 (
    .CLK(CLK), .RW(id_ex_register_1_rw_2), .WB(id_ex_register_1_wb_2), .WBA(id_ex_register_1_wba_2),
    .MS(id_ex_register_1_ms_2), .A(id_ex_register_1_msadd_2), .D(id_ex_register_1_a_2), .ALURES(alu_1_out),
    .RW_2(exdmr_1_rw_2), .WB_2(exdmr_1_wb_2), .WBA_2(EXDMRD), .MS_2(exdmr_1_ms_2), .A_2(exdmr_1_a_2),
    .D_2(exdmr_1_d_2), .ALURES_2(exdmr_1_alures_2));
  Register #(.width(1)) register_3 (.D(exdmr_1_rw_2), .Q(register_3_q), .clk(CLK));  // open: en, clr
  Register #(.width(1)) register_4 (.D(exdmr_1_wb_2), .Q(register_4_q), .clk(CLK));  // open: en, clr
  Register #(.width(2)) register_5 (.D(EXDMRD), .Q(register_5_q), .clk(CLK));  // open: en, clr
  Register register_6 (.D(exdmr_1_alures_2), .Q(register_6_q), .clk(CLK));  // open: en, clr
  Register register_7 (.D(ram_2_data), .Q(register_7_q), .clk(CLK));  // open: en, clr
  RAM #(.bus("separate")) ram_2 (
    .addr(exdmr_1_a_2), .din(exdmr_1_d_2), .data(ram_2_data), .str(exdmr_1_ms_2), .clk(CLK), .ld(1'b1));  // open: sel, clr
  Multiplexer #(.width(8)) multiplexer_12 (
    .in0(register_6_q), .in1(register_7_q), .out(multiplexer_12_out), .sel(register_4_q));  // open: en

  // Other names for the same wires on the sheet: R0[7:0] = A; R1[7:0] = A_2; R2[7:0] = A_3; R3[7:0] = A_4

  // Notes on the sheet:
  //   DM/WB Registers
endmodule

// ID
module Inst_Decoder (
  input  [15:0] Instruction,
  output [5:0] OP,
  output [1:0] RS,
  output [1:0] RT,
  output [1:0] RD,
  output [3:0] Fun,
  output [5:0] Immediate,
  output [7:0] Address
);


  assign Address = Instruction[7:0];
  assign Fun = Instruction[3:0];
  assign Immediate = Instruction[5:0];
  assign OP = Instruction[15:10];
  assign RD = Instruction[5:4];
  assign RS = Instruction[9:8];
  assign RT = Instruction[7:6];
endmodule

// Control
module Controller (
  input  [5:0] OP_Code,
  output WSel,
  output WBSel,
  output Msw,
  output ASel,
  output ALUSel,
  output [3:0] ALUFun,
  output waSel
);

  wire and_4_out, nor_1_out, not_1_out, not_2_out, not_3_out, not_4_out, not_5_out, not_6_out, not_7_out,
       not_8_out, not_9_out;

  not not_1 (not_1_out, OP_Code[1]);
  not not_2 (not_2_out, OP_Code[2]);
  not not_3 (not_3_out, OP_Code[3]);
  and and_1 (Msw, OP_Code[0], not_1_out, not_2_out, not_3_out, OP_Code[4], OP_Code[5]);
  not not_4 (not_4_out, OP_Code[4]);
  not not_5 (not_5_out, OP_Code[0]);
  not not_6 (not_6_out, OP_Code[1]);
  not not_7 (not_7_out, OP_Code[2]);
  not not_8 (not_8_out, OP_Code[3]);
  and and_2 (ASel, not_4_out, OP_Code[5]);
  and and_3 (WBSel, not_5_out, not_6_out, not_7_out, not_8_out, OP_Code[4], OP_Code[5]);
  not not_9 (not_9_out, OP_Code[4]);
  or or_1 (ALUSel, OP_Code[0], OP_Code[1], OP_Code[2], OP_Code[3], OP_Code[4], OP_Code[5]);
  nor nor_1 (nor_1_out, OP_Code[0], OP_Code[1], OP_Code[2], OP_Code[3], OP_Code[4], OP_Code[5]);
  and and_4 (and_4_out, not_9_out, OP_Code[5]);
  or or_2 (WSel, nor_1_out, and_4_out, WBSel);
  or or_3 (waSel, ASel, WBSel);

  assign ALUFun = OP_Code[3:0];

  // Other names for the same wires on the sheet: OP0 = OP_Code[0]; OP1 = OP_Code[1]; OP2 = OP_Code[2];
  //   OP3 = OP_Code[3]; OP4 = OP_Code[4]; OP5 = OP_Code[5]
endmodule

module Staller (
  input  ID_EX_RW,
  input  [1:0] ID_EX_rd,
  input  [1:0] EX_DM_rd,
  input  EX_DM_RW,
  input  [15:0] Instruction_Next,
  output PCw,
  output IF_IDw,
  output Bubble
);

  wire and_1_out, and_2_out, and_3_out, and_4_out, and_6_out, and_7_out, and_8_out, and_9_out, and_10_out,
       comparator_1_eq, comparator_2_eq, comparator_3_eq, comparator_4_eq, comparator_5_eq, comparator_6_eq,
       comparator_7_eq, comparator_8_eq, comparator_9_eq, comparator_10_eq, IStall, not_1_out, or_1_out,
       or_2_out, or_3_out, or_4_out, RStall, StoreStall;
  wire [1:0] RS, RT;
  wire [5:0] OP;

  Comparator #(.width(6)) comparator_1 (.a(OP), .b({6{1'b0}}), .eq(comparator_1_eq));  // open: gt, lt
  Comparator #(.width(2)) comparator_2 (.a(RT), .b(ID_EX_rd), .eq(comparator_2_eq));  // open: gt, lt
  Comparator #(.width(2)) comparator_3 (.a(RT), .b(EX_DM_rd), .eq(comparator_3_eq));  // open: gt, lt
  Comparator #(.width(2)) comparator_4 (.a(RS), .b(ID_EX_rd), .eq(comparator_4_eq));  // open: gt, lt
  Comparator #(.width(2)) comparator_5 (.a(RS), .b(EX_DM_rd), .eq(comparator_5_eq));  // open: gt, lt
  Inst_Decoder inst_decoder_1 (
    .Instruction(Instruction_Next), .OP(OP), .RS(RS), .RT(RT));  // open: RD, Fun, Immediate, Address
  and and_1 (and_1_out, comparator_2_eq, ID_EX_RW);
  and and_2 (and_2_out, comparator_3_eq, EX_DM_RW);
  and and_3 (and_3_out, comparator_4_eq, ID_EX_RW);
  and and_4 (and_4_out, comparator_5_eq, EX_DM_RW);
  or or_1 (or_1_out, and_1_out, and_2_out, and_3_out, and_4_out);
  and and_5 (RStall, comparator_1_eq, or_1_out);
  Comparator #(.width(6)) comparator_6 (.a(OP), .b(6'b110001), .eq(comparator_6_eq));  // open: gt, lt
  Comparator #(.width(2)) comparator_7 (.a(RS), .b(ID_EX_rd), .eq(comparator_7_eq));  // open: gt, lt
  Comparator #(.width(2)) comparator_8 (.a(RS), .b(EX_DM_rd), .eq(comparator_8_eq));  // open: gt, lt
  not not_1 (not_1_out, OP[4]);
  Comparator #(.width(2)) comparator_9 (.a(RT), .b(ID_EX_rd), .eq(comparator_9_eq));  // open: gt, lt
  Comparator #(.width(2)) comparator_10 (.a(RT), .b(EX_DM_rd), .eq(comparator_10_eq));  // open: gt, lt
  and and_6 (and_6_out, comparator_7_eq, ID_EX_RW);
  and and_7 (and_7_out, comparator_8_eq, EX_DM_RW);
  or or_2 (or_2_out, RStall, IStall, StoreStall);
  and and_8 (and_8_out, not_1_out, OP[5]);
  and and_9 (and_9_out, comparator_9_eq, ID_EX_RW);
  and and_10 (and_10_out, comparator_10_eq, EX_DM_RW);
  not not_2 (IF_IDw, or_2_out);
  or or_3 (or_3_out, and_6_out, and_7_out);
  not not_3 (Bubble, IF_IDw);
  and and_11 (StoreStall, comparator_6_eq, or_3_out);
  or or_4 (or_4_out, and_9_out, and_10_out);
  and and_12 (IStall, and_8_out, or_4_out);

  assign PCw = IF_IDw;

  // Other names for the same wires on the sheet: D1[1:0] = ID_EX_rd; D2[1:0] = EX_DM_rd; M1 = ID_EX_RW; M2 = EX_DM_RW
endmodule

// ID/EX R
module ID_EX_Register (
  input  CLK,
  input  RW,
  input  WB,
  input  [1:0] WBA,
  input  MS,
  input  [7:0] MSADD,
  input  ASEL,
  input  ALU_SEL,
  input  [3:0] IALU,
  input  [7:0] A,
  input  [7:0] B,
  input  [7:0] IMM,
  input  [3:0] RALU,
  output RW_2,
  output WB_2,
  output [1:0] WBA_2,
  output MS_2,
  output [7:0] MSADD_2,
  output ASEL_2,
  output ALU_SEL_2,
  output [3:0] IALU_2,
  output [7:0] A_2,
  output [7:0] B_2,
  output [7:0] IMM_2,
  output [3:0] RALU_2
);

  Register #(.width(1)) register_1 (.D(RW), .Q(RW_2), .clk(CLK));  // open: en, clr
  Register #(.width(1)) register_2 (.D(WB), .Q(WB_2), .clk(CLK));  // open: en, clr
  Register #(.width(2)) register_3 (.D(WBA), .Q(WBA_2), .clk(CLK));  // open: en, clr
  Register #(.width(1)) register_4 (.D(MS), .Q(MS_2), .clk(CLK));  // open: en, clr
  Register register_5 (.D(MSADD), .Q(MSADD_2), .clk(CLK));  // open: en, clr
  Register #(.width(1)) register_6 (.D(ASEL), .Q(ASEL_2), .clk(CLK));  // open: en, clr
  Register #(.width(1)) register_7 (.D(ALU_SEL), .Q(ALU_SEL_2), .clk(CLK));  // open: en, clr
  Register #(.width(4)) register_8 (.D(IALU), .Q(IALU_2), .clk(CLK));  // open: en, clr
  Register register_9 (.D(A), .Q(A_2), .clk(CLK));  // open: en, clr
  Register register_10 (.D(B), .Q(B_2), .clk(CLK));  // open: en, clr
  Register register_11 (.D(IMM), .Q(IMM_2), .clk(CLK));  // open: en, clr
  Register #(.width(4)) register_12 (.D(RALU), .Q(RALU_2), .clk(CLK));  // open: en, clr
endmodule

module EXDMR (
  input  CLK,
  input  RW,
  input  WB,
  input  [1:0] WBA,
  input  MS,
  input  [7:0] A,
  input  [7:0] D,
  input  [7:0] ALURES,
  output RW_2,
  output WB_2,
  output [1:0] WBA_2,
  output MS_2,
  output [7:0] A_2,
  output [7:0] D_2,
  output [7:0] ALURES_2
);

  Register #(.width(1)) register_1 (.D(RW), .Q(RW_2), .clk(CLK));  // open: en, clr
  Register #(.width(1)) register_2 (.D(WB), .Q(WB_2), .clk(CLK));  // open: en, clr
  Register #(.width(2)) register_3 (.D(WBA), .Q(WBA_2), .clk(CLK));  // open: en, clr
  Register #(.width(1)) register_4 (.D(MS), .Q(MS_2), .clk(CLK));  // open: en, clr
  Register register_5 (.D(A), .Q(A_2), .clk(CLK));  // open: en, clr
  Register register_6 (.D(D), .Q(D_2), .clk(CLK));  // open: en, clr
  Register register_7 (.D(ALURES), .Q(ALURES_2), .clk(CLK));  // open: en, clr
endmodule
