// Logisim project 1901cs75_assign7.circ as structural Verilog: 2 circuits, main circuit Booth's Algo 4-bit
module Booth_s_Algo_4_bit (
  input  [3:0] M,
  input  [3:0] Q,
  input  in_3,
  output [7:0] Output
);

  wire A_S, CLK, multiplexer_2_out, Q_1_prime, S;
  wire [0:0] Q0_Q_1;
  wire [2:0] Count_prime, multiplexer_6_out, register_4_q;
  wire [3:0] A_prime, add_sub_1_result, multiplexer_1_out, multiplexer_3_out, Q_prime;
  wire [8:0] multiplexer_5_out;

  Multiplexer #(.width(4)) multiplexer_1 (.in0(4'b0000), .in1(A_prime), .out(multiplexer_1_out), .sel(S));  // open: en
  Register #(.width(4)) register_1 (.D(multiplexer_1_out), .Q(Output[7:4]), .clk(CLK), .clr(in_3));  // open: en
  Multiplexer multiplexer_2 (.in0(1'b0), .in1(Q_1_prime), .out(multiplexer_2_out), .sel(S));  // open: en
  Clock Clock (.out(CLK));
  Multiplexer #(.width(4)) multiplexer_3 (.in0(Q), .in1(Q_prime), .out(multiplexer_3_out), .sel(S));  // open: en
  Register #(.width(4)) register_2 (.D(multiplexer_3_out), .Q(Output[3:0]), .clk(CLK), .clr(in_3));  // open: en
  Register #(.width(1)) register_3 (.D(multiplexer_2_out), .Q(Q0_Q_1[0]), .clk(CLK), .clr(in_3));  // open: en
  Add_Sub add_sub_1 (.A(Output[7:4]), .B(M), .Subt(A_S), .Result(add_sub_1_result));  // open: Overflow
  Multiplexer #(.select(2)) multiplexer_4 (
    .in0(1'b1), .in1(1'b0), .in2(1'b1), .in3(1'b1), .out(A_S), .sel({Output[0], Q0_Q_1[0]}));  // open: en
  Multiplexer #(.select(2), .width(9)) multiplexer_5 (
    .in0({Output, Q0_Q_1[0]}), .in1({add_sub_1_result, Output[3:0], Q0_Q_1[0]}),
    .in2({add_sub_1_result, Output[3:0], Q0_Q_1[0]}), .in3({Output, Q0_Q_1[0]}), .out(multiplexer_5_out),
    .sel({Output[0], Q0_Q_1[0]}));  // open: en
  Shifter #(.width(9), .shift("ar")) shifter_1 (
    .in(multiplexer_5_out), .\dist (4'b0001), .out({A_prime, Q_prime, Q_1_prime}));
  Multiplexer #(.width(3)) multiplexer_6 (
    .in0(3'b100), .in1(Count_prime), .out(multiplexer_6_out), .sel(S));  // open: en
  Register #(.width(3)) register_4 (.D(multiplexer_6_out), .Q(register_4_q), .clk(CLK), .clr(in_3));  // open: en
  Subtractor #(.width(3)) subtractor_1 (.a(register_4_q), .b(3'b001), .out(Count_prime));  // open: bin, bout
  or or_1 (S, register_4_q[0], register_4_q[1], register_4_q[2]);

  // Other names for the same wires on the sheet: Q_1 = Q0_Q_1[0]; Q0 = Output[0]; Q0_Q_1[1] = Output[0];
  //   Q_t[3:0] = Output[3:0]; A[3:0] = Output[7:4]; Reset = in_3
endmodule

// A/S
module Add_Sub (
  input  [3:0] A,
  input  [3:0] B,
  input  Subt,
  output [3:0] Result,
  output Overflow
);

  wire [3:0] multiplexer_1_out, not_1_out;

  assign not_1_out = ~B;  // NOT_Gate not_1, 4 bits wide
  Multiplexer #(.width(4)) multiplexer_1 (.in0(B), .in1(not_1_out), .out(multiplexer_1_out), .sel(Subt));  // open: en
  Adder #(.width(4)) adder_1 (.a(A), .b(multiplexer_1_out), .out(Result), .cin(Subt), .cout(Overflow));
endmodule
