// Logisim project p3.circ as structural Verilog: 1 circuit, main circuit main
module main (
  input  B,
  input  A,
  output Y
);

  wire transistor_1_out;

  Transistor transistor_1 (.in(1'b1), .out(transistor_1_out), .gate(A));
  Transistor #(.\type ("n")) transistor_2 (.in(1'b0), .out(transistor_1_out), .gate(A));
  Transistor #(.\type ("n")) transistor_3 (.in(transistor_1_out), .out(Y), .gate(B));
  Transistor transistor_4 (.in(A), .out(Y), .gate(B));
endmodule
