// Logisim project p4.circ as structural Verilog: 1 circuit, main circuit main
module main (
  input  A,
  input  B,
  input  C,
  output Y
);

  wire transistor_1_out, transistor_2_out;

  Transistor #(.\type ("n")) transistor_1 (.in(1'b1), .out(transistor_1_out), .gate(A));
  Transistor #(.\type ("n")) transistor_2 (.in(transistor_1_out), .out(transistor_2_out), .gate(B));
  Transistor #(.\type ("n")) transistor_3 (.in(transistor_2_out), .out(Y), .gate(C));
  Transistor transistor_4 (.in(1'b0), .out(Y), .gate(B));
  Transistor transistor_5 (.in(1'b0), .out(Y), .gate(C));
  Transistor transistor_6 (.in(1'b0), .out(Y), .gate(A));
endmodule
