// Logisim project p5.circ as structural Verilog: 1 circuit, main circuit main
module main (
  input  A,
  input  B,
  input  C,
  input  D,
  output Y
);

  wire transistor_4_out, transistor_5_out, transistor_6_out;

  Transistor #(.\type ("n")) transistor_1 (.in(1'b1), .out(Y), .gate(A));
  Transistor #(.\type ("n")) transistor_2 (.in(1'b1), .out(Y), .gate(B));
  Transistor #(.\type ("n")) transistor_3 (.in(1'b1), .out(Y), .gate(C));
  Transistor transistor_4 (.in(1'b0), .out(transistor_4_out), .gate(A));
  Transistor transistor_5 (.in(transistor_4_out), .out(transistor_5_out), .gate(B));
  Transistor transistor_6 (.in(transistor_5_out), .out(transistor_6_out), .gate(C));
  Transistor transistor_7 (.in(transistor_6_out), .out(Y), .gate(D));
  Transistor #(.\type ("n")) transistor_8 (.in(1'b1), .out(Y), .gate(D));
endmodule
