// Logisim project NOR.circ as structural Verilog: 1 circuit, main circuit main
module main (
  input  A,
  input  B,
  output out_3
);

  wire transistor_1_out;

  Transistor transistor_1 (.in(1'b1), .out(transistor_1_out), .gate(A));
  Transistor transistor_2 (.in(transistor_1_out), .out(out_3), .gate(B));
  Transistor #(.\type ("n")) transistor_3 (.in(1'b0), .out(out_3), .gate(A));
  Transistor #(.\type ("n")) transistor_4 (.in(1'b0), .out(out_3), .gate(B));
endmodule
