// Logisim project XOR.circ as structural Verilog: 1 circuit, main circuit main
module main (
  input  A,
  input  B,
  output out_3
);

  wire transistor_1_out;

  Transistor #(.\type ("n")) transistor_1 (.in(1'b0), .out(transistor_1_out), .gate(B));
  Transistor transistor_2 (.in(1'b1), .out(transistor_1_out), .gate(B));
  Transistor #(.\type ("n")) transistor_3 (.in(transistor_1_out), .out(out_3), .gate(A));
  Transistor transistor_4 (.in(B), .out(out_3), .gate(A));
endmodule
