// Logisim project p1.circ as structural Verilog: 1 circuit, main circuit main
module main (
  input  A,
  input  B,
  input  C,
  input  D,
  output Y
);

  wire transistor_1_out, transistor_2_out, transistor_3_out;

  Transistor transistor_1 (.in(1'b1), .out(transistor_1_out), .gate(A));
  Transistor transistor_2 (.in(transistor_1_out), .out(transistor_2_out), .gate(B));
  Transistor transistor_3 (.in(transistor_2_out), .out(transistor_3_out), .gate(C));
  Transistor transistor_4 (.in(transistor_3_out), .out(Y), .gate(D));
  Pull_Resistor pull_resistor_1 (.node(Y));

  // Notes on the sheet:
  //   SERIES PMOS
endmodule
