// Logisim project p2.circ as structural Verilog: 1 circuit, main circuit main
module main (
  input  A,
  input  B,
  input  C,
  input  D,
  input  E,
  output Y3,
  output Y1,
  output Y2,
  output Y4
);

  wire pull_resistor_2_node, transistor_2_out, transistor_3_out, transistor_4_out, transistor_5_out,
       transistor_7_out, transistor_8_out, transistor_9_out, transistor_10_out, transistor_12_out;

  Pull_Resistor #(.pull(1)) pull_resistor_1 (.node(Y1));
  Transistor #(.\type ("n")) transistor_1 (.in(transistor_2_out), .out(Y1), .gate(A));
  Transistor #(.\type ("n")) transistor_2 (.in(transistor_3_out), .out(transistor_2_out), .gate(B));
  Transistor #(.\type ("n")) transistor_3 (.in(transistor_4_out), .out(transistor_3_out), .gate(C));
  Transistor #(.\type ("n")) transistor_4 (.in(transistor_5_out), .out(transistor_4_out), .gate(D));
  Transistor #(.\type ("n")) transistor_5 (.in(1'b0), .out(transistor_5_out), .gate(E));
  Pull_Resistor #(.pull(1)) pull_resistor_2 (.node(pull_resistor_2_node));
  Transistor #(.\type ("n")) transistor_6 (.in(transistor_7_out), .out(pull_resistor_2_node), .gate(A));
  Transistor #(.\type ("n")) transistor_7 (.in(transistor_8_out), .out(transistor_7_out), .gate(B));
  Transistor #(.\type ("n")) transistor_8 (.in(transistor_9_out), .out(transistor_8_out), .gate(C));
  Transistor #(.\type ("n")) transistor_9 (.in(transistor_10_out), .out(transistor_9_out), .gate(D));
  Transistor #(.\type ("n")) transistor_10 (.in(1'b0), .out(transistor_10_out), .gate(E));
  Pull_Resistor #(.pull(1)) pull_resistor_3 (.node(Y2));
  Transistor #(.\type ("n")) transistor_11 (.in(1'b0), .out(Y2), .gate(pull_resistor_2_node));
  Transistor #(.\type ("n")) transistor_12 (.in(1'b0), .out(transistor_12_out), .gate(A));
  Transistor #(.\type ("n")) transistor_13 (.in(1'b0), .out(transistor_12_out), .gate(B));
  Transistor #(.\type ("n")) transistor_14 (.in(1'b0), .out(Y4), .gate(A));
  Pull_Resistor #(.pull(1)) pull_resistor_4 (.node(transistor_12_out));
  Transistor #(.\type ("n")) transistor_15 (.in(1'b0), .out(transistor_12_out), .gate(C));
  Transistor #(.\type ("n")) transistor_16 (.in(1'b0), .out(Y4), .gate(B));
  Transistor #(.\type ("n")) transistor_17 (.in(1'b0), .out(Y4), .gate(C));
  Transistor #(.\type ("n")) transistor_18 (.in(1'b0), .out(transistor_12_out), .gate(D));
  Transistor #(.\type ("n")) transistor_19 (.in(1'b0), .out(Y4), .gate(D));
  Pull_Resistor #(.pull(1)) pull_resistor_5 (.node(Y3));
  Transistor #(.\type ("n")) transistor_20 (.in(1'b0), .out(Y3), .gate(transistor_12_out));
  Transistor #(.\type ("n")) transistor_21 (.in(1'b0), .out(transistor_12_out), .gate(E));
  Pull_Resistor #(.pull(1)) pull_resistor_6 (.node(Y4));
  Transistor #(.\type ("n")) transistor_22 (.in(1'b0), .out(Y4), .gate(E));

  // Notes on the sheet:
  //   5 Input NMOS NAND
  //   5 Input NMOS AND
  //   5 Input NMOS OR
  //   5 Input NMOS NOR
endmodule
