// Logisim project p3.circ as structural Verilog: 1 circuit, main circuit main
module main (
  input  A,
  input  C,
  input  E,
  input  B,
  input  D,
  output Y
);

  wire transistor_2_out, transistor_3_out, transistor_5_out, transistor_9_out;

  Transistor #(.\type ("n")) transistor_1 (.in(transistor_2_out), .out(Y), .gate(A));
  Transistor #(.\type ("n")) transistor_2 (.in(1'b0), .out(transistor_2_out), .gate(B));
  Transistor transistor_3 (.in(1'b1), .out(transistor_3_out), .gate(B));
  Transistor transistor_4 (.in(1'b1), .out(transistor_3_out), .gate(A));
  Transistor transistor_5 (.in(transistor_3_out), .out(transistor_5_out), .gate(C));
  Transistor transistor_6 (.in(transistor_3_out), .out(transistor_5_out), .gate(D));
  Transistor transistor_7 (.in(transistor_5_out), .out(Y), .gate(E));
  Transistor #(.\type ("n")) transistor_8 (.in(transistor_9_out), .out(Y), .gate(C));
  Transistor #(.\type ("n")) transistor_9 (.in(1'b0), .out(transistor_9_out), .gate(D));
  Transistor #(.\type ("n")) transistor_10 (.in(1'b0), .out(Y), .gate(E));

  // Notes on the sheet:
  //   ~(A.B+C.D+E
endmodule
