// Logisim project p4.circ as structural Verilog: 1 circuit, main circuit main
module main (
  input  A,
  input  C,
  input  E,
  input  B,
  input  D,
  output Y
);

  wire transistor_1_out, transistor_2_out, transistor_3_out, transistor_5_out, transistor_9_out;

  Transistor #(.\type ("n")) transistor_1 (.in(transistor_2_out), .out(transistor_1_out), .gate(A));
  Transistor #(.\type ("n")) transistor_2 (.in(1'b0), .out(transistor_2_out), .gate(B));
  Transistor transistor_3 (.in(1'b1), .out(transistor_3_out), .gate(A));
  Transistor transistor_4 (.in(1'b1), .out(transistor_3_out), .gate(B));
  Transistor transistor_5 (.in(transistor_3_out), .out(transistor_5_out), .gate(C));
  Transistor transistor_6 (.in(transistor_3_out), .out(transistor_5_out), .gate(D));
  Transistor transistor_7 (.in(transistor_5_out), .out(transistor_1_out), .gate(E));
  Transistor #(.\type ("n")) transistor_8 (.in(transistor_9_out), .out(transistor_1_out), .gate(C));
  Transistor #(.\type ("n")) transistor_9 (.in(1'b0), .out(transistor_9_out), .gate(D));
  Transistor #(.\type ("n")) transistor_10 (.in(1'b0), .out(transistor_1_out), .gate(E));
  Transistor transistor_11 (.in(1'b1), .out(Y), .gate(transistor_1_out));
  Transistor #(.\type ("n")) transistor_12 (.in(1'b0), .out(Y), .gate(transistor_1_out));

  // Notes on the sheet:
  //   A.B+C.D+E
endmodule
