// Logisim project p5.circ as structural Verilog: 1 circuit, main circuit main
module main (
  input  A,
  input  B,
  input  C,
  output Y
);

  wire main_1_out_3;

  AND_main main_1 (.A(A), .B(B), .out_3(main_1_out_3));
  OR_main main_2 (.in_1(main_1_out_3), .in_2(C), .out_3(Y));
endmodule
