// Logisim project p6.circ as structural Verilog: 1 circuit, main circuit main
module main (
  input  A,
  input  B,
  input  C,
  input  D,
  output Y
);

  wire main_1_out_3, main_2_out_3;

  AND_main main_1 (.A(B), .B(C), .out_3(main_1_out_3));
  OR_main main_2 (.in_1(A), .in_2(main_1_out_3), .out_3(main_2_out_3));
  OR_main main_3 (.in_1(main_2_out_3), .in_2(D), .out_3(Y));
endmodule
