// Logisim project Q1.circ as structural Verilog: 1 circuit, main circuit main
module main (
  input  [7:0] in_1,
  input  _1_Write___0_Read,
  input  [7:0] A,
  input  [7:0] Address,
  input  in_5,
  input  Enable,
  output [7:0] out_7,
  output [7:0] out_8
);

  wire not_1_out;

  ROM rom_1 (.addr(A), .data(out_7), .sel(in_5));
  assign out_8 = _1_Write___0_Read ? in_1 : 8'bz;  // Controlled_Buffer controlled_buffer_1
  not not_1 (not_1_out, _1_Write___0_Read);
  RAM #(.bus("asynch")) ram_1 (.addr(Address), .data(out_8), .sel(Enable), .ld(not_1_out));  // open: clr

  // Notes on the sheet:
  //   ROM
  //   RAM
endmodule
