// Logisim project Q2.circ as structural Verilog: 2 circuits, main circuit ROM
module ROM (
  input  [20:0] Address,
  output [31:0] out_2
);

  wire decoder_1_out0, decoder_1_out1, decoder_1_out2, decoder_1_out3;

  Decoder #(.select(2), .enable("false")) decoder_1 (
    .out0(decoder_1_out0), .out1(decoder_1_out1), .out2(decoder_1_out2), .out3(decoder_1_out3),
    .sel(Address[20:19]));
  ROM_part #(.addrWidth(19)) rom_1 (.addr(Address[18:0]), .data(out_2[31:24]), .sel(decoder_1_out0));
  ROM_part #(.addrWidth(19)) rom_2 (.addr(Address[18:0]), .data(out_2[31:24]), .sel(decoder_1_out1));
  ROM_part #(.addrWidth(19)) rom_3 (.addr(Address[18:0]), .data(out_2[31:24]), .sel(decoder_1_out2));
  ROM_part #(.addrWidth(19)) rom_4 (.addr(Address[18:0]), .data(out_2[31:24]), .sel(decoder_1_out3));
  ROM_part #(.addrWidth(19)) rom_5 (.addr(Address[18:0]), .data(out_2[23:16]), .sel(decoder_1_out0));
  ROM_part #(.addrWidth(19)) rom_6 (.addr(Address[18:0]), .data(out_2[23:16]), .sel(decoder_1_out1));
  ROM_part #(.addrWidth(19)) rom_7 (.addr(Address[18:0]), .data(out_2[23:16]), .sel(decoder_1_out2));
  ROM_part #(.addrWidth(19)) rom_8 (.addr(Address[18:0]), .data(out_2[23:16]), .sel(decoder_1_out3));
  ROM_part #(.addrWidth(19)) rom_9 (.addr(Address[18:0]), .data(out_2[15:8]), .sel(decoder_1_out0));
  ROM_part #(.addrWidth(19)) rom_10 (.addr(Address[18:0]), .data(out_2[15:8]), .sel(decoder_1_out1));
  ROM_part #(.addrWidth(19)) rom_11 (.addr(Address[18:0]), .data(out_2[15:8]), .sel(decoder_1_out2));
  ROM_part #(.addrWidth(19)) rom_12 (.addr(Address[18:0]), .data(out_2[15:8]), .sel(decoder_1_out3));
  ROM_part #(.addrWidth(19)) rom_13 (.addr(Address[18:0]), .data(out_2[7:0]), .sel(decoder_1_out0));
  ROM_part #(.addrWidth(19)) rom_14 (.addr(Address[18:0]), .data(out_2[7:0]), .sel(decoder_1_out1));
  ROM_part #(.addrWidth(19)) rom_15 (.addr(Address[18:0]), .data(out_2[7:0]), .sel(decoder_1_out2));
  ROM_part #(.addrWidth(19)) rom_16 (.addr(Address[18:0]), .data(out_2[7:0]), .sel(decoder_1_out3));
endmodule

module RAM (
  input  [20:0] Address,
  input  Load,
  input  Store,
  input  [31:0] W,
  output [31:0] R
);

  wire Clock_out, decoder_1_out0, decoder_1_out1, decoder_1_out2, decoder_1_out3;

  Decoder #(.select(2), .enable("false")) decoder_1 (
    .out0(decoder_1_out0), .out1(decoder_1_out1), .out2(decoder_1_out2), .out3(decoder_1_out3),
    .sel(Address[20:19]));
  Clock Clock (.out(Clock_out));
  RAM_part #(.addrWidth(19), .bus("separate")) ram_1 (
    .addr(Address[18:0]), .din(W[31:24]), .data(R[31:24]), .str(Store), .sel(decoder_1_out0),
    .clk(Clock_out), .ld(Load));  // open: clr
  RAM_part #(.addrWidth(19), .bus("separate")) ram_2 (
    .addr(Address[18:0]), .din(W[31:24]), .data(R[31:24]), .str(Store), .sel(decoder_1_out1),
    .clk(Clock_out), .ld(Load));  // open: clr
  RAM_part #(.addrWidth(19), .bus("separate")) ram_3 (
    .addr(Address[18:0]), .din(W[31:24]), .data(R[31:24]), .str(Store), .sel(decoder_1_out2),
    .clk(Clock_out), .ld(Load));  // open: clr
  RAM_part #(.addrWidth(19), .bus("separate")) ram_4 (
    .addr(Address[18:0]), .din(W[31:24]), .data(R[31:24]), .str(Store), .sel(decoder_1_out3),
    .clk(Clock_out), .ld(Load));  // open: clr
  RAM_part #(.addrWidth(19), .bus("separate")) ram_5 (
    .addr(Address[18:0]), .din(W[23:16]), .data(R[23:16]), .str(Store), .sel(decoder_1_out0),
    .clk(Clock_out), .ld(Load));  // open: clr
  RAM_part #(.addrWidth(19), .bus("separate")) ram_6 (
    .addr(Address[18:0]), .din(W[23:16]), .data(R[23:16]), .str(Store), .sel(decoder_1_out1),
    .clk(Clock_out), .ld(Load));  // open: clr
  RAM_part #(.addrWidth(19), .bus("separate")) ram_7 (
    .addr(Address[18:0]), .din(W[23:16]), .data(R[23:16]), .str(Store), .sel(decoder_1_out2),
    .clk(Clock_out), .ld(Load));  // open: clr
  RAM_part #(.addrWidth(19), .bus("separate")) ram_8 (
    .addr(Address[18:0]), .din(W[23:16]), .data(R[23:16]), .str(Store), .sel(decoder_1_out3),
    .clk(Clock_out), .ld(Load));  // open: clr
  RAM_part #(.addrWidth(19), .bus("separate")) ram_9 (
    .addr(Address[18:0]), .din(W[15:8]), .data(R[15:8]), .str(Store), .sel(decoder_1_out0), .clk(Clock_out),
    .ld(Load));  // open: clr
  RAM_part #(.addrWidth(19), .bus("separate")) ram_10 (
    .addr(Address[18:0]), .din(W[15:8]), .data(R[15:8]), .str(Store), .sel(decoder_1_out1), .clk(Clock_out),
    .ld(Load));  // open: clr
  RAM_part #(.addrWidth(19), .bus("separate")) ram_11 (
    .addr(Address[18:0]), .din(W[15:8]), .data(R[15:8]), .str(Store), .sel(decoder_1_out2), .clk(Clock_out),
    .ld(Load));  // open: clr
  RAM_part #(.addrWidth(19), .bus("separate")) ram_12 (
    .addr(Address[18:0]), .din(W[15:8]), .data(R[15:8]), .str(Store), .sel(decoder_1_out3), .clk(Clock_out),
    .ld(Load));  // open: clr
  RAM_part #(.addrWidth(19), .bus("separate")) ram_13 (
    .addr(Address[18:0]), .din(W[7:0]), .data(R[7:0]), .str(Store), .sel(decoder_1_out0), .clk(Clock_out),
    .ld(Load));  // open: clr
  RAM_part #(.addrWidth(19), .bus("separate")) ram_14 (
    .addr(Address[18:0]), .din(W[7:0]), .data(R[7:0]), .str(Store), .sel(decoder_1_out1), .clk(Clock_out),
    .ld(Load));  // open: clr
  RAM_part #(.addrWidth(19), .bus("separate")) ram_15 (
    .addr(Address[18:0]), .din(W[7:0]), .data(R[7:0]), .str(Store), .sel(decoder_1_out2), .clk(Clock_out),
    .ld(Load));  // open: clr
  RAM_part #(.addrWidth(19), .bus("separate")) ram_16 (
    .addr(Address[18:0]), .din(W[7:0]), .data(R[7:0]), .str(Store), .sel(decoder_1_out3), .clk(Clock_out),
    .ld(Load));  // open: clr
endmodule
