// Logisim project Q3.circ as structural Verilog: 4 circuits, main circuit main
module main (
  input  Clear,
  output [15:0] Input1,
  output [15:0] Input2,
  output [15:0] Output__sum,
  output [15:0] Data,
  output [15:0] Data_2,
  output [15:0] Data_3
);

  wire and_1_out, Clk, controller_1_count_enable, controller_1_irld, controller_1_mem_write_enable,
       controller_1_rd_enable, controller_1_read_enable, controller_1_rpenable, controller_1_rqenable,
       controller_1_rwen, controller_1_select, not_1_out, not_2_out;
  wire [2:0] controller_1_alu_sel;
  wire [3:0] controller_1_rpaddr, controller_1_rqaddr, controller_1_waddr;
  wire [7:0] controller_1_data;
  wire [15:0] controlled_buffer_1_out, counter_1_q, IR_q, multiplexer_1_out, rom_1_data;

  Clock Clock (.out(Clk));
  Counter #(.width(16), .max('hffff)) counter_1 (
    .count(controller_1_count_enable), .Q(counter_1_q), .clk(Clk), .clr(Clear));  // open: load, D, carry
  ROM #(.addrWidth(16), .dataWidth(16)) rom_1 (.addr(counter_1_q), .data(rom_1_data), .sel(controller_1_rd_enable));
  Register_part #(.width(16)) IR (.D(rom_1_data), .en(controller_1_irld), .Q(IR_q), .clk(Clk));  // open: clr
  Controller controller_1 (
    .Clock(Clk), .IRld(controller_1_irld), .Rd_Enable(controller_1_rd_enable),
    .Count_Enable(controller_1_count_enable), .Instruction(IR_q), .Data(controller_1_data),
    .Read_Enable(controller_1_read_enable), .Mem_Write_Enable(controller_1_mem_write_enable),
    .select(controller_1_select), .Waddr(controller_1_waddr), .RWen(controller_1_rwen),
    .Rpaddr(controller_1_rpaddr), .Rpenable(controller_1_rpenable), .Rqaddr(controller_1_rqaddr),
    .Rqenable(controller_1_rqenable), .ALU_Sel(controller_1_alu_sel));
  not not_1 (not_1_out, controller_1_mem_write_enable);
  and and_1 (and_1_out, controller_1_read_enable, not_1_out);
  not not_2 (not_2_out, and_1_out);
  assign controlled_buffer_1_out = not_2_out ? Data : 16'bz;  // Controlled_Buffer controlled_buffer_1
  Multiplexer #(.width(16)) multiplexer_1 (
    .in0(Data_2), .in1(controlled_buffer_1_out), .out(multiplexer_1_out), .sel(controller_1_select));  // open: en
  Register register_1 (
    .Write_Address(controller_1_waddr), .Write_Enable(controller_1_rwen),
    .Read_Address_1(controller_1_rpaddr), .Read_Enable_1(controller_1_rpenable),
    .Read_Address_2(controller_1_rqaddr), .Read_Enable_2(controller_1_rqenable), .Clock(Clk),
    .Data(multiplexer_1_out), .Read_1(Data), .Read_2(Data_3), .Data_2(Input1), .Data_3(Input2),
    .Data_4(Output__sum));  // open: Clear
  ALU alu_1 (
    .Select(controller_1_alu_sel), .Input_1(Data), .Input_2(Data_3), .Output(Data_2));  // open: Overflow_in_Addition, Subtraction_Result_is_Negative
  RAM #(.dataWidth(16)) ram_1 (
    .addr(controller_1_data), .data(controlled_buffer_1_out), .clk(Clk), .ld(and_1_out));  // open: sel, clr

  // Notes on the sheet:
  //   contents of rom_1 (hex, n*v repeats v):
  //   0 101 2201 1202
endmodule

module Controller (
  input  [15:0] Instruction,
  input  Clock,
  output [7:0] Data,
  output Read_Enable,
  output Mem_Write_Enable,
  output select,
  output IRld,
  output [3:0] Waddr,
  output RWen,
  output Rd_Enable,
  output [3:0] Rpaddr,
  output Count_Enable,
  output Rpenable,
  output [3:0] Rqaddr,
  output Rqenable,
  output [2:0] ALU_Sel
);

  wire [1:0] \wait ;

  Multiplexer #(.select(2)) multiplexer_1 (
    .in0(1'b1), .in1(1'b0), .in2(1'b0), .in3(1'b0), .out(IRld), .sel(\wait ));  // open: en
  Multiplexer #(.select(2)) multiplexer_2 (
    .in0(1'b1), .in1(1'b0), .in2(1'b0), .in3(1'b0), .out(Rd_Enable), .sel(\wait ));  // open: en
  Multiplexer #(.select(2)) multiplexer_3 (
    .in0(1'b1), .in1(1'b0), .in2(1'b0), .in3(1'b0), .out(Count_Enable), .sel(\wait ));  // open: en
  Counter #(.width(2), .max('h2)) counter_1 (.Q(\wait ), .clk(Clock));  // open: load, D, count, carry, clr
  Multiplexer #(.select(2)) multiplexer_4 (
    .in0(1'b1), .in1(1'b0), .in2(1'b1), .in3(1'b0), .out(Read_Enable), .sel(Instruction[13:12]));  // open: en
  Multiplexer #(.select(2)) multiplexer_5 (
    .in0(1'b0), .in1(1'b1), .in2(1'b0), .in3(1'b0), .out(Mem_Write_Enable), .sel(Instruction[13:12]));  // open: en
  Multiplexer #(.select(2)) multiplexer_6 (
    .in0(1'b1), .in1(1'b0), .in2(1'b0), .in3(1'b0), .out(select), .sel(Instruction[13:12]));  // open: en
  Multiplexer #(.select(2)) multiplexer_7 (
    .in0(1'b1), .in1(1'b0), .in2(1'b1), .in3(1'b0), .out(RWen), .sel(Instruction[13:12]));  // open: en
  Multiplexer #(.select(2)) multiplexer_8 (
    .in0(1'b0), .in1(1'b1), .in2(1'b1), .in3(1'b0), .out(Rpenable), .sel(Instruction[13:12]));  // open: en
  Multiplexer #(.select(2)) multiplexer_9 (
    .in0(1'b0), .in1(1'b0), .in2(1'b1), .in3(1'b0), .out(Rqenable), .sel(Instruction[13:12]));  // open: en
  Multiplexer #(.select(2), .width(4)) multiplexer_10 (
    .in0(Instruction[7:4]), .in1(Instruction[11:8]), .in2(Instruction[7:4]), .in3(Instruction[7:4]),
    .out(Rpaddr), .sel(Instruction[13:12]));  // open: en

  assign ALU_Sel = 3'b000;
  assign Data = Instruction[7:0];
  assign Rqaddr = Instruction[3:0];
  assign Waddr = Instruction[11:8];

  // Other names for the same wires on the sheet: D[7:0] = Instruction[7:0]; R1[3:0] = Instruction[3:0];
  //   R0[3:0] = Instruction[7:4]; R2[3:0] = Instruction[11:8]; op[1:0] = Instruction[13:12]
endmodule

module ALU (
  input  [15:0] Input_1,
  input  [15:0] Input_2,
  input  [2:0] Select,
  output Overflow_in_Addition,
  output Subtraction_Result_is_Negative,
  output [15:0] Output
);

  wire comparator_1_eq, comparator_2_gt, comparator_3_lt;
  wire [15:0] adder_1_out, and_1_out, bit_extender_1_out, multiplexer_1_out, multiplexer_2_out, or_1_out,
       subtractor_1_out, xor_1_out;

  Adder #(.width(16)) adder_1 (.a(Input_1), .b(Input_2), .out(adder_1_out), .cout(Overflow_in_Addition));  // open: cin
  Subtractor #(.width(16)) subtractor_1 (
    .a(Input_1), .b(Input_2), .out(subtractor_1_out), .bout(Subtraction_Result_is_Negative));  // open: bin
  assign and_1_out = Input_1 & Input_2;  // AND_Gate and_1, 16 bits wide
  assign or_1_out = Input_1 | Input_2;  // OR_Gate or_1, 16 bits wide
  assign xor_1_out = Input_1 ^ Input_2;  // XOR_Gate xor_1, 16 bits wide
  Comparator #(.width(16)) comparator_1 (.a(Input_1), .b(Input_2), .eq(comparator_1_eq));  // open: gt, lt
  Comparator #(.width(16)) comparator_2 (.a(Input_1), .b(Input_2), .gt(comparator_2_gt));  // open: eq, lt
  Comparator #(.width(16)) comparator_3 (.a(Input_1), .b(Input_2), .lt(comparator_3_lt));  // open: gt, eq
  assign bit_extender_1_out = {{15{1'b0}}, comparator_1_eq};  // Bit_Extender bit_extender_1
  Multiplexer #(.width(16)) multiplexer_1 (
    .in0(Input_1), .in1(Input_2), .out(multiplexer_1_out), .sel(comparator_2_gt));  // open: en
  Multiplexer #(.width(16)) multiplexer_2 (
    .in0(Input_1), .in1(Input_2), .out(multiplexer_2_out), .sel(comparator_3_lt));  // open: en
  Multiplexer #(.select(3), .width(16)) multiplexer_3 (
    .in0(adder_1_out), .in1(subtractor_1_out), .in2(and_1_out), .in3(or_1_out), .in4(xor_1_out),
    .in5(bit_extender_1_out), .in6(multiplexer_1_out), .in7(multiplexer_2_out), .out(Output), .sel(Select));  // open: en

  // Other names for the same wires on the sheet: A[15:0] = Input_1; B[15:0] = Input_2
endmodule

// Reg
module Register (
  input  [15:0] Data,
  input  [3:0] Write_Address,
  input  Write_Enable,
  input  [3:0] Read_Address_1,
  input  Read_Enable_1,
  input  [3:0] Read_Address_2,
  input  Read_Enable_2,
  input  Clear,
  input  Clock,
  output [15:0] Data_2,
  output [15:0] Data_3,
  output [15:0] Data_4,
  output [15:0] Read_1,
  output [15:0] Read_2
);

  wire and_1_out, and_2_out, and_3_out, and_4_out, and_5_out, and_6_out, and_7_out, and_8_out, and_9_out,
       and_10_out, and_11_out, and_12_out, and_13_out, and_14_out, and_15_out, and_16_out, decoder_1_out0,
       decoder_1_out1, decoder_1_out2, decoder_1_out3, decoder_1_out4, decoder_1_out5, decoder_1_out6,
       decoder_1_out7, decoder_1_out8, decoder_1_out9, decoder_1_out10, decoder_1_out11, decoder_1_out12,
       decoder_1_out13, decoder_1_out14, decoder_1_out15;
  wire [15:0] register_4_q, register_5_q, register_6_q, register_7_q, register_8_q, register_9_q,
       register_10_q, register_11_q, register_12_q, register_13_q, register_14_q, register_15_q,
       register_16_q;

  Decoder #(.select(4)) decoder_1 (
    .out0(decoder_1_out0), .out1(decoder_1_out1), .out2(decoder_1_out2), .out3(decoder_1_out3),
    .out4(decoder_1_out4), .out5(decoder_1_out5), .out6(decoder_1_out6), .out7(decoder_1_out7),
    .out8(decoder_1_out8), .out9(decoder_1_out9), .out10(decoder_1_out10), .out11(decoder_1_out11),
    .out12(decoder_1_out12), .out13(decoder_1_out13), .out14(decoder_1_out14), .out15(decoder_1_out15),
    .sel(Write_Address));  // open: en
  and and_1 (and_1_out, decoder_1_out0, Write_Enable);
  and and_2 (and_2_out, decoder_1_out1, Write_Enable);
  and and_3 (and_3_out, decoder_1_out2, Write_Enable);
  and and_4 (and_4_out, decoder_1_out3, Write_Enable);
  and and_5 (and_5_out, decoder_1_out4, Write_Enable);
  and and_6 (and_6_out, decoder_1_out5, Write_Enable);
  and and_7 (and_7_out, decoder_1_out6, Write_Enable);
  and and_8 (and_8_out, decoder_1_out7, Write_Enable);
  and and_9 (and_9_out, decoder_1_out8, Write_Enable);
  and and_10 (and_10_out, decoder_1_out9, Write_Enable);
  and and_11 (and_11_out, decoder_1_out10, Write_Enable);
  and and_12 (and_12_out, decoder_1_out11, Write_Enable);
  and and_13 (and_13_out, decoder_1_out12, Write_Enable);
  and and_14 (and_14_out, decoder_1_out13, Write_Enable);
  and and_15 (and_15_out, decoder_1_out14, Write_Enable);
  and and_16 (and_16_out, decoder_1_out15, Write_Enable);
  Register_part #(.width(16)) register_1 (.D(Data), .en(and_1_out), .Q(Data_2), .clk(Clock), .clr(Clear));
  Register_part #(.width(16)) register_2 (.D(Data), .en(and_2_out), .Q(Data_3), .clk(Clock), .clr(Clear));
  Register_part #(.width(16)) register_3 (.D(Data), .en(and_3_out), .Q(Data_4), .clk(Clock), .clr(Clear));
  Register_part #(.width(16)) register_4 (.D(Data), .en(and_4_out), .Q(register_4_q), .clk(Clock), .clr(Clear));
  Register_part #(.width(16)) register_5 (.D(Data), .en(and_5_out), .Q(register_5_q), .clk(Clock), .clr(Clear));
  Register_part #(.width(16)) register_6 (.D(Data), .en(and_6_out), .Q(register_6_q), .clk(Clock), .clr(Clear));
  Register_part #(.width(16)) register_7 (.D(Data), .en(and_7_out), .Q(register_7_q), .clk(Clock), .clr(Clear));
  Register_part #(.width(16)) register_8 (.D(Data), .en(and_8_out), .Q(register_8_q), .clk(Clock), .clr(Clear));
  Register_part #(.width(16)) register_9 (.D(Data), .en(and_9_out), .Q(register_9_q), .clk(Clock), .clr(Clear));
  Register_part #(.width(16)) register_10 (.D(Data), .en(and_10_out), .Q(register_10_q), .clk(Clock), .clr(Clear));
  Register_part #(.width(16)) register_11 (.D(Data), .en(and_11_out), .Q(register_11_q), .clk(Clock), .clr(Clear));
  Register_part #(.width(16)) register_12 (.D(Data), .en(and_12_out), .Q(register_12_q), .clk(Clock), .clr(Clear));
  Register_part #(.width(16)) register_13 (.D(Data), .en(and_13_out), .Q(register_13_q), .clk(Clock), .clr(Clear));
  Register_part #(.width(16)) register_14 (.D(Data), .en(and_14_out), .Q(register_14_q), .clk(Clock), .clr(Clear));
  Register_part #(.width(16)) register_15 (.D(Data), .en(and_15_out), .Q(register_15_q), .clk(Clock), .clr(Clear));
  Register_part #(.width(16)) register_16 (.D(Data), .en(and_16_out), .Q(register_16_q), .clk(Clock), .clr(Clear));
  Multiplexer #(.select(4), .width(16)) multiplexer_1 (
    .in0(Data_2), .in1(Data_3), .in2(Data_4), .in3(register_4_q), .in4(register_5_q), .in5(register_6_q),
    .in6(register_7_q), .in7(register_8_q), .in8(register_9_q), .in9(register_10_q), .in10(register_11_q),
    .in11(register_12_q), .in12(register_13_q), .in13(register_14_q), .in14(register_15_q),
    .in15(register_16_q), .out(Read_1), .sel(Read_Address_1), .en(Read_Enable_1));
  Multiplexer #(.select(4), .width(16)) multiplexer_2 (
    .in0(Data_2), .in1(Data_3), .in2(Data_4), .in3(register_4_q), .in4(register_5_q), .in5(register_6_q),
    .in6(register_7_q), .in7(register_8_q), .in8(register_9_q), .in9(register_10_q), .in10(register_11_q),
    .in11(register_12_q), .in12(register_13_q), .in13(register_14_q), .in14(register_15_q),
    .in15(register_16_q), .out(Read_2), .sel(Read_Address_2), .en(Read_Enable_2));

  // Other names for the same wires on the sheet: R1 = Read_Enable_1; R2 = Read_Enable_2

  // Notes on the sheet:
  //   A 16x16 Register File
  //   With 2 Read port and 1 Write Port
endmodule
