// Logisim project p1.circ as structural Verilog: 1 circuit, main circuit main
module main (
  input  y,
  input  z,
  input  x,
  input  w,
  output Output
);

  wire and_1_out, and_2_out, and_3_out, and_4_out, not_1_out, not_2_out, not_3_out, not_4_out;

  not not_1 (not_1_out, z);
  not not_2 (not_2_out, y);
  not not_3 (not_3_out, x);
  not not_4 (not_4_out, w);
  and and_1 (and_1_out, w, not_3_out, not_2_out);
  and and_2 (and_2_out, not_4_out, not_1_out, y);
  and and_3 (and_3_out, x, z, y);
  and and_4 (and_4_out, y, x, w);
  or or_1 (Output, and_1_out, and_2_out, and_3_out, and_4_out);

  // Notes on the sheet:
  //   w.x'.y'+y.w'.z'+y.x.z+y.x.w
endmodule
