// Logisim project p10.circ as structural Verilog: 3 circuits, main circuit main
module main (
  input  a0,
  input  b0,
  input  a1,
  input  b1,
  output S0,
  output S1,
  output Carry
);

  wire and_1_out, and_2_out, and_3_out, xor_2_out;

  xor xor_1 (S0, b0, a0);
  and and_1 (and_1_out, b0, a0);
  xor xor_2 (xor_2_out, a1, b1);
  and and_2 (and_2_out, xor_2_out, and_1_out);
  and and_3 (and_3_out, a1, b1);
  xor xor_3 (S1, xor_2_out, and_1_out);
  or or_1 (Carry, and_2_out, and_3_out);
endmodule

module Half_Adder (
  input  A,
  input  B,
  output Sum,
  output Carry
);

  xor xor_1 (Sum, B, A);
  and and_1 (Carry, B, A);
endmodule

module Full_Adder (
  input  A,
  input  B,
  input  C,
  output Sum,
  output Carry
);

  wire and_1_out, and_2_out, xor_1_out;

  xor xor_1 (xor_1_out, A, B);
  and and_1 (and_1_out, xor_1_out, C);
  and and_2 (and_2_out, A, B);
  xor xor_2 (Sum, xor_1_out, C);
  or or_1 (Carry, and_1_out, and_2_out);
endmodule
