// Logisim project p11.circ as structural Verilog: 2 circuits, main circuit main
module main (
  input  in_1,
  input  in_2,
  input  in_3,
  output sum,
  output carry
);

  wire not_1_out;

  not not_1 (not_1_out, 1'b0);
  _8X1_Multiplexer u_8x1_multiplexer_1 (
    .i0(1'b0), .i1(not_1_out), .i2(not_1_out), .i3(1'b0), .i4(not_1_out), .i5(1'b0), .i6(1'b0),
    .i7(not_1_out), .s0(in_1), .s1(in_2), .s2(in_3), .Output(sum));
  _8X1_Multiplexer u_8x1_multiplexer_2 (
    .i0(1'b0), .i1(1'b0), .i2(1'b0), .i3(not_1_out), .i4(1'b0), .i5(not_1_out), .i6(not_1_out),
    .i7(not_1_out), .s0(in_1), .s1(in_2), .s2(in_3), .Output(carry));

  // Other names for the same wires on the sheet: a = in_1; b = in_2; c = in_3
endmodule

module _8X1_Multiplexer (
  input  i0,
  input  i1,
  input  i2,
  input  i3,
  input  i4,
  input  i5,
  input  i6,
  input  i7,
  input  s0,
  input  s1,
  input  s2,
  output Output
);

  wire and_1_out, and_2_out, and_3_out, and_4_out, and_5_out, and_6_out, and_7_out, and_8_out, not_1_out,
       not_2_out, not_3_out;

  not not_1 (not_1_out, s0);
  not not_2 (not_2_out, s1);
  not not_3 (not_3_out, s2);
  and and_1 (and_1_out, i0, not_3_out, not_2_out, not_1_out);
  and and_2 (and_2_out, i1, not_3_out, not_2_out, s0);
  and and_3 (and_3_out, i2, not_3_out, s1, not_1_out);
  and and_4 (and_4_out, i3, not_3_out, s1, s0);
  and and_5 (and_5_out, i4, s2, not_2_out, not_1_out);
  and and_6 (and_6_out, i5, s2, not_2_out, s0);
  and and_7 (and_7_out, i6, s2, s1, not_1_out);
  and and_8 (and_8_out, i7, s2, s1, s0);
  or or_1 (Output, and_1_out, and_2_out, and_3_out, and_4_out, and_5_out, and_6_out, and_7_out, and_8_out);
endmodule
