// Logisim project p4.circ as structural Verilog: 1 circuit, main circuit main
module main (
  input  in_1,
  input  in_2,
  input  A,
  input  B,
  input  C,
  input  D,
  output Output
);

  wire and_1_out, and_2_out, and_3_out, and_4_out, not_1_out, not_2_out, not_3_out, not_4_out, or_1_out,
       or_2_out, s0_out, s1_out, s2_out, s3_out;

  not not_1 (not_1_out, in_1);
  not not_2 (not_2_out, in_2);
  and s1 (s1_out, in_2, not_1_out);
  and s2 (s2_out, not_2_out, in_1);
  and s3 (s3_out, in_1, in_2);
  and s0 (s0_out, not_1_out, not_2_out);
  or or_1 (or_1_out, s2_out, s3_out);
  or or_2 (or_2_out, s1_out, s3_out);
  not not_3 (not_3_out, or_2_out);
  not not_4 (not_4_out, or_1_out);
  and and_1 (and_1_out, or_1_out, or_2_out, D);
  and and_2 (and_2_out, not_3_out, or_1_out, C);
  and and_3 (and_3_out, not_4_out, or_2_out, B);
  and and_4 (and_4_out, not_4_out, not_3_out, A);
  or or_3 (Output, and_1_out, and_2_out, and_3_out, and_4_out);
endmodule
