// Logisim project p6.circ as structural Verilog: 2 circuits, main circuit main
module main (
  input  d0,
  input  c0,
  input  b0,
  input  a0,
  input  d1,
  input  s0,
  input  s1,
  input  c1,
  input  b1,
  input  a1,
  input  d2,
  input  c2,
  input  b2,
  input  a2,
  input  d3,
  input  c3,
  input  b3,
  input  a3,
  output Y0,
  output Y1,
  output Y2,
  output Y3
);

  _4X1_MUX u_4x1_mux_1 (.i0(d0), .i1(c0), .i2(b0), .i3(a0), .s1(s0), .s0(s1), .d(Y0));
  _4X1_MUX u_4x1_mux_2 (.i0(d1), .i1(c1), .i2(b1), .i3(a1), .s1(s0), .s0(s1), .d(Y1));
  _4X1_MUX u_4x1_mux_3 (.i0(d2), .i1(c2), .i2(b2), .i3(a2), .s1(s0), .s0(s1), .d(Y2));
  _4X1_MUX u_4x1_mux_4 (.i0(d3), .i1(c3), .i2(b3), .i3(a3), .s1(s0), .s0(s1), .d(Y3));
endmodule

module _4X1_MUX (
  input  i0,
  input  i1,
  input  i2,
  input  i3,
  input  s1,
  input  s0,
  output d
);

  wire and_1_out, and_2_out, and_3_out, and_4_out, not_1_out, not_2_out;

  not not_1 (not_1_out, s1);
  not not_2 (not_2_out, s0);
  and and_1 (and_1_out, i0, not_1_out, not_2_out);
  and and_2 (and_2_out, i1, not_1_out, s0);
  and and_3 (and_3_out, i2, s1, not_2_out);
  and and_4 (and_4_out, i3, s0, s1);
  or or_1 (d, and_1_out, and_2_out, and_3_out, and_4_out);
endmodule
