// Logisim project p7.circ as structural Verilog: 1 circuit, main circuit main
module main (
  input  i0,
  input  i1,
  input  i2,
  input  i3,
  input  i4,
  input  i5,
  input  i6,
  input  i7,
  input  s2,
  input  s1,
  input  s0,
  output Output
);

  wire _0_out, _1_out, _2_out, _3_out, _4_out, _5_out, _6_out, _7_out, not_1_out, not_2_out, not_3_out;

  not not_1 (not_1_out, s0);
  not not_2 (not_2_out, s1);
  not not_3 (not_3_out, s2);
  and _0 (_0_out, i0, not_3_out, not_2_out, not_1_out);
  and _1 (_1_out, i1, not_3_out, not_2_out, s0);
  and _2 (_2_out, i2, not_3_out, s1, not_1_out);
  and _3 (_3_out, i3, not_3_out, s1, s0);
  and _4 (_4_out, i4, s2, not_2_out, not_1_out);
  and _5 (_5_out, i5, s2, not_2_out, s0);
  and _6 (_6_out, i6, s2, s1, not_1_out);
  and _7 (_7_out, i7, s2, s1, s0);
  or or_1 (Output, _0_out, _1_out, _2_out, _3_out, _4_out, _5_out, _6_out, _7_out);

  // Notes on the sheet:
  //   8x1 MUX
endmodule
