// Logisim project p9.circ as structural Verilog: 3 circuits, main circuit Full Adder
module main (
  input  b0,
  input  a0,
  input  a1,
  input  b1,
  output S0,
  output S1,
  output Carry
);

  wire half_adder_1_carry;

  Half_Adder half_adder_1 (.A(a0), .B(b0), .Sum(S0), .Carry(half_adder_1_carry));
  Full_Adder full_adder_1 (.A(half_adder_1_carry), .B(a1), .C(b1), .Sum(S1), .Carry(Carry));
endmodule

module Half_Adder (
  input  A,
  input  B,
  output Sum,
  output Carry
);

  xor xor_1 (Sum, B, A);
  and and_1 (Carry, B, A);

  // Notes on the sheet:
  //   A^B
endmodule

module Full_Adder (
  input  A,
  input  B,
  input  C,
  output Sum,
  output Carry
);

  wire and_1_out, and_2_out, and_3_out, xor_1_out;

  xor xor_1 (xor_1_out, A, B);
  and and_1 (and_1_out, A, B);
  and and_2 (and_2_out, B, C);
  and and_3 (and_3_out, C, A);
  xor xor_2 (Sum, xor_1_out, C);
  or or_1 (Carry, and_1_out, and_2_out, and_3_out);

  // Notes on the sheet:
  //   A^B^C
  //   A.B+B.C+C.A
endmodule
