// Logisim project 4bit adder.circ as structural Verilog: 1 circuit, main circuit main
module main (
  input  b0,
  input  a0,
  input  b3,
  input  a3,
  input  b2,
  input  a2,
  input  b1,
  input  a1,
  input  c_in,
  output s3,
  output s2,
  output s1,
  output s0,
  output c_out
);

  wire adder_2_cout, adder_3_cout, adder_4_cout;

  Adder #(.width(1)) adder_1 (.a(a3), .b(b3), .out(s3), .cin(adder_2_cout), .cout(c_out));
  Adder #(.width(1)) adder_2 (.a(a2), .b(b2), .out(s2), .cin(adder_3_cout), .cout(adder_2_cout));
  Adder #(.width(1)) adder_3 (.a(a1), .b(b1), .out(s1), .cin(adder_4_cout), .cout(adder_3_cout));
  Adder #(.width(1)) adder_4 (.a(a0), .b(b0), .out(s0), .cin(c_in), .cout(adder_4_cout));
endmodule
