// Logisim project p1.circ as structural Verilog: 2 circuits, main circuit main
module main (
  input  a0,
  input  a1,
  input  a2,
  input  a3,
  input  a4,
  input  a5,
  input  a6,
  input  a7,
  input  b0,
  input  b1,
  input  b2,
  input  b3,
  input  b4,
  input  b5,
  input  b6,
  input  b7,
  input  in_17,
  output C,
  output s0,
  output s1,
  output s2,
  output s3,
  output s4,
  output s5,
  output s6,
  output s7
);

  wire full_adder_1_carry, full_adder_2_carry, full_adder_3_carry, full_adder_4_carry, full_adder_5_carry,
       full_adder_6_carry, full_adder_7_carry;

  Full_Adder_Full_Adder full_adder_1 (.A(a0), .B(b0), .C(in_17), .Sum(s0), .Carry(full_adder_1_carry));
  Full_Adder_Full_Adder full_adder_2 (.A(a1), .B(b1), .C(full_adder_1_carry), .Sum(s1), .Carry(full_adder_2_carry));
  Full_Adder_Full_Adder full_adder_3 (.A(a2), .B(b2), .C(full_adder_2_carry), .Sum(s2), .Carry(full_adder_3_carry));
  Full_Adder_Full_Adder full_adder_4 (.A(a3), .B(b3), .C(full_adder_3_carry), .Sum(s3), .Carry(full_adder_4_carry));
  Full_Adder_Full_Adder full_adder_5 (.A(a4), .B(b4), .C(full_adder_4_carry), .Sum(s4), .Carry(full_adder_5_carry));
  Full_Adder_Full_Adder full_adder_6 (.A(a5), .B(b5), .C(full_adder_5_carry), .Sum(s5), .Carry(full_adder_6_carry));
  Full_Adder_Full_Adder full_adder_7 (.A(a6), .B(b6), .C(full_adder_6_carry), .Sum(s6), .Carry(full_adder_7_carry));
  Full_Adder_Full_Adder full_adder_8 (.A(a7), .B(b7), .C(full_adder_7_carry), .Sum(s7), .Carry(C));

  // Notes on the sheet:
  //   carry=0 for first bit
  //   Input: A=a7a6a5a4a3a2a1a0   B=b7b6b5b4b3b2b1b0
  //   Output: C s7s6s5s4s3s2s1s0
endmodule

module Full_Adder (
  input  A,
  input  B,
  input  C,
  output Sum,
  output Carry
);

  wire and_1_out, and_2_out, and_3_out, xor_1_out;

  xor xor_1 (xor_1_out, A, B);
  and and_1 (and_1_out, A, B);
  and and_2 (and_2_out, B, C);
  and and_3 (and_3_out, C, A);
  xor xor_2 (Sum, xor_1_out, C);
  or or_1 (Carry, and_1_out, and_2_out, and_3_out);

  // Notes on the sheet:
  //   A^B^C
  //   A.B+B.C+C.A
endmodule
