// Logisim project p2.circ as structural Verilog: 1 circuit, main circuit main
module main (
  input  b7,
  input  b6,
  input  b5,
  input  b4,
  input  b3,
  input  b2,
  input  b1,
  input  b0,
  input  Addition_Substration,
  input  a7,
  input  a6,
  input  a5,
  input  a4,
  input  a3,
  input  a2,
  input  a1,
  input  a0,
  output s7,
  output s4,
  output s3,
  output s0,
  output s6,
  output s5,
  output s2,
  output s1,
  output Overflow
);

  wire main_1_c_out, main_2_c_out, xor_1_out, xor_3_out, xor_4_out, xor_5_out, xor_6_out, xor_7_out,
       xor_8_out, xor_9_out, xor_10_out, xor_11_out;

  xor xor_1 (xor_1_out, b7, a7);
  xor xor_2 (Overflow, xor_1_out, xor_4_out);
  xor xor_3 (xor_3_out, b7, Addition_Substration);
  xor xor_4 (xor_4_out, main_1_c_out, s7);
  xor xor_5 (xor_5_out, b6, Addition_Substration);
  xor xor_6 (xor_6_out, b5, Addition_Substration);
  _4bit_adder_main main_1 (
    .c_out(main_1_c_out), .b3(a7), .a3(xor_3_out), .b2(a6), .a2(xor_5_out), .b1(a5), .a1(xor_6_out), .b0(a4),
    .a0(xor_7_out), .s3(s7), .s2(s6), .s1(s5), .s0(s4), .c_in(main_2_c_out));
  xor xor_7 (xor_7_out, b4, Addition_Substration);
  xor xor_8 (xor_8_out, b3, Addition_Substration);
  xor xor_9 (xor_9_out, b2, Addition_Substration);
  xor xor_10 (xor_10_out, b1, Addition_Substration);
  _4bit_adder_main main_2 (
    .c_out(main_2_c_out), .b3(a3), .a3(xor_8_out), .b2(a2), .a2(xor_9_out), .b1(a1), .a1(xor_10_out),
    .b0(a0), .a0(xor_11_out), .s3(s3), .s2(s2), .s1(s1), .s0(s0), .c_in(Addition_Substration));
  xor xor_11 (xor_11_out, b0, Addition_Substration);
endmodule
