// Logisim project p3.circ as structural Verilog: 6 circuits, main circuit main
module main (
  input  [3:0] A,
  input  [3:0] B,
  input  s1,
  input  s0,
  output [3:0] Output
);

  wire [3:0] and_1_output, n4_bit_adder_subtractor_1_sum_difference, or_1_output;

  _4_bit_Adder_Subtractor u_4_bit_adder_subtractor_1 (
    .A(A), .B(B), .Cin(s0), .Sum_Difference(n4_bit_adder_subtractor_1_sum_difference));  // open: Cout
  AND and_1 (.A(A), .B(B), .Output(and_1_output));
  OR or_1 (.A(A), .B(B), .Output(or_1_output));
  _4_x_1_Multiplexer u_4_x_1_multiplexer_1 (
    .A(n4_bit_adder_subtractor_1_sum_difference), .B(n4_bit_adder_subtractor_1_sum_difference),
    .C(and_1_output), .D(or_1_output), .s1(s1), .s0(s0), .Output(Output));

  // Notes on the sheet:
  //   00 -Add
  //   01 -Subtract
  //   10 -> AND
  //   11 -> OR
endmodule

// A/S
module _4_bit_Adder_Subtractor (
  input  Cin,
  input  [3:0] A,
  input  [3:0] B,
  output [3:0] Sum_Difference,
  output Cout
);

  wire full_adder_1_cout, full_adder_2_cout, full_adder_3_cout, xor_1_out, xor_2_out, xor_3_out, xor_4_out;

  xor xor_1 (xor_1_out, B[0], Cin);
  xor xor_2 (xor_2_out, B[1], Cin);
  xor xor_3 (xor_3_out, B[2], Cin);
  xor xor_4 (xor_4_out, B[3], Cin);
  Full_Adder full_adder_1 (.a(A[0]), .b(xor_1_out), .Cin(Cin), .Cout(full_adder_1_cout), .Sum(Sum_Difference[0]));
  Full_Adder full_adder_2 (
    .a(A[1]), .b(xor_2_out), .Cin(full_adder_1_cout), .Cout(full_adder_2_cout), .Sum(Sum_Difference[1]));
  Full_Adder full_adder_3 (
    .a(A[2]), .b(xor_3_out), .Cin(full_adder_2_cout), .Cout(full_adder_3_cout), .Sum(Sum_Difference[2]));
  Full_Adder full_adder_4 (.a(A[3]), .b(xor_4_out), .Cin(full_adder_3_cout), .Cout(Cout), .Sum(Sum_Difference[3]));
endmodule

// 4x1
module _4_x_1_Multiplexer (
  input  [3:0] A,
  input  [3:0] B,
  input  [3:0] C,
  input  [3:0] D,
  input  s1,
  input  s0,
  output [3:0] Output
);

  wire [3:0] and_1_out, and_2_out, and_3_out, and_4_out, not_1_out, not_2_out;

  assign not_1_out = ~{4{s1}};  // NOT_Gate not_1, 4 bits wide
  assign not_2_out = ~{4{s0}};  // NOT_Gate not_2, 4 bits wide
  assign and_1_out = A & not_1_out & not_2_out;  // AND_Gate and_1, 4 bits wide
  assign and_2_out = B & not_1_out & {4{s0}};  // AND_Gate and_2, 4 bits wide
  assign and_3_out = C & {4{s1}} & not_2_out;  // AND_Gate and_3, 4 bits wide
  assign and_4_out = D & {4{s1}} & {4{s0}};  // AND_Gate and_4, 4 bits wide
  assign Output = and_1_out | and_2_out | and_3_out | and_4_out;  // OR_Gate or_1, 4 bits wide
endmodule

module AND (
  input  [3:0] A,
  input  [3:0] B,
  output [3:0] Output
);

  and and_1 (Output[1], A[1], B[1]);
  and and_2 (Output[0], A[0], B[0]);
  and and_3 (Output[2], A[2], B[2]);
  and and_4 (Output[3], A[3], B[3]);
endmodule

module OR (
  input  [3:0] A,
  input  [3:0] B,
  output [3:0] Output
);

  or or_1 (Output[0], A[0], B[0]);
  or or_2 (Output[1], A[1], B[1]);
  or or_3 (Output[2], A[2], B[2]);
  or or_4 (Output[3], A[3], B[3]);
endmodule

module Full_Adder (
  input  Cin,
  input  a,
  input  b,
  output Sum,
  output Cout
);

  wire and_1_out, and_2_out, xor_1_out;

  and and_1 (and_1_out, a, b);
  xor xor_1 (xor_1_out, a, b);
  or or_1 (Cout, and_1_out, and_2_out);
  and and_2 (and_2_out, xor_1_out, Cin);
  xor xor_2 (Sum, xor_1_out, Cin);
endmodule
