// Logisim project p4.circ as structural Verilog: 4 circuits, main circuit main
module main (
  input  [7:0] A,
  input  [7:0] B,
  input  S
);

  wire [0:0] n8_bit_adder_subtractor_1_overflow;
  wire [7:0] n2_1_multiplexer_1_sum, n8_bit_adder_subtractor_1_sum, not_1_out;

  assign not_1_out = ~B;  // NOT_Gate not_1, 8 bits wide
  _2_1_Multiplexer u_2_1_multiplexer_1 (.A(B), .B(not_1_out), .S(S), .Sum(n2_1_multiplexer_1_sum));
  _8_Bit_Adder_Subtractor u_8_bit_adder_subtractor_1 (
    .OverFlow(n8_bit_adder_subtractor_1_overflow[0]), .A(A), .B(n2_1_multiplexer_1_sum),
    .Sum(n8_bit_adder_subtractor_1_sum), .Carry_In(S));
  Hex_Digit_Display hex_digit_display_1 (.value({3'b000, n8_bit_adder_subtractor_1_overflow[0]}));  // open: dp
  Hex_Digit_Display hex_digit_display_2 (.value(n8_bit_adder_subtractor_1_sum[7:4]));  // open: dp
  Hex_Digit_Display hex_digit_display_3 (.value(n8_bit_adder_subtractor_1_sum[3:0]));  // open: dp

  // Notes on the sheet:
  //   S=0 A+B
  //   S=1 A-B
  //   OverFlow
  //   Hex-Value
  //   OUTPUT
endmodule

module Single_Bit_Full_Adder (
  input  Carry_In,
  input  A,
  input  B,
  output Sum,
  output Carry_out
);

  wire and_1_out, and_2_out, xor_1_out;

  and and_1 (and_1_out, A, B);
  or or_1 (Carry_out, and_1_out, and_2_out);
  xor xor_1 (xor_1_out, A, B);
  and and_2 (and_2_out, xor_1_out, Carry_In);
  xor xor_2 (Sum, Carry_In, xor_1_out);
endmodule

// A/S
module _8_Bit_Adder_Subtractor (
  input  [7:0] A,
  input  [7:0] B,
  input  Carry_In,
  output OverFlow,
  output [7:0] Sum
);

  wire single_bit_full_adder_1_carry_out, single_bit_full_adder_2_carry_out,
       single_bit_full_adder_3_carry_out, single_bit_full_adder_4_carry_out,
       single_bit_full_adder_5_carry_out, single_bit_full_adder_6_carry_out,
       single_bit_full_adder_7_carry_out, single_bit_full_adder_8_carry_out, xor_1_out, xor_2_out;

  xor xor_1 (xor_1_out, A[7], B[7]);
  xor xor_2 (xor_2_out, single_bit_full_adder_1_carry_out, Sum[7]);
  xor xor_3 (OverFlow, xor_1_out, xor_2_out);
  Single_Bit_Full_Adder single_bit_full_adder_1 (
    .A(B[7]), .B(A[7]), .Carry_In(single_bit_full_adder_2_carry_out),
    .Carry_out(single_bit_full_adder_1_carry_out), .Sum(Sum[7]));
  Single_Bit_Full_Adder single_bit_full_adder_2 (
    .A(B[6]), .B(A[6]), .Carry_In(single_bit_full_adder_3_carry_out),
    .Carry_out(single_bit_full_adder_2_carry_out), .Sum(Sum[6]));
  Single_Bit_Full_Adder single_bit_full_adder_3 (
    .A(B[5]), .B(A[5]), .Carry_In(single_bit_full_adder_5_carry_out),
    .Carry_out(single_bit_full_adder_3_carry_out), .Sum(Sum[5]));
  Single_Bit_Full_Adder single_bit_full_adder_4 (
    .A(B[3]), .B(A[3]), .Carry_In(single_bit_full_adder_6_carry_out),
    .Carry_out(single_bit_full_adder_4_carry_out), .Sum(Sum[3]));
  Single_Bit_Full_Adder single_bit_full_adder_5 (
    .A(B[4]), .B(A[4]), .Carry_In(single_bit_full_adder_4_carry_out),
    .Carry_out(single_bit_full_adder_5_carry_out), .Sum(Sum[4]));
  Single_Bit_Full_Adder single_bit_full_adder_6 (
    .A(B[2]), .B(A[2]), .Carry_In(single_bit_full_adder_7_carry_out),
    .Carry_out(single_bit_full_adder_6_carry_out), .Sum(Sum[2]));
  Single_Bit_Full_Adder single_bit_full_adder_7 (
    .A(B[1]), .B(A[1]), .Carry_In(single_bit_full_adder_8_carry_out),
    .Carry_out(single_bit_full_adder_7_carry_out), .Sum(Sum[1]));
  Single_Bit_Full_Adder single_bit_full_adder_8 (
    .A(B[0]), .B(A[0]), .Carry_In(Carry_In), .Carry_out(single_bit_full_adder_8_carry_out), .Sum(Sum[0]));
endmodule

module _2_1_Multiplexer (
  input  [7:0] A,
  input  [7:0] B,
  input  S,
  output [7:0] Sum
);

  wire [7:0] and_1_out, and_2_out, not_1_out;

  assign not_1_out = ~{8{S}};  // NOT_Gate not_1, 8 bits wide
  assign and_1_out = A & not_1_out;  // AND_Gate and_1, 8 bits wide
  assign and_2_out = B & {8{S}};  // AND_Gate and_2, 8 bits wide
  assign Sum = and_1_out | and_2_out;  // OR_Gate or_1, 8 bits wide
endmodule
