// Logisim project 1_bit_comparator.circ as structural Verilog: 1 circuit, main circuit main
module main (
  input  a,
  input  b,
  input  igt,
  input  ieq,
  input  ilt,
  output ogt,
  output oeq,
  output olt
);

  wire and_1_out, and_2_out, not_1_out, not_2_out, xnor_1_out;

  not not_1 (not_1_out, b);
  not not_2 (not_2_out, a);
  and and_1 (and_1_out, a, not_1_out, ieq);
  and and_2 (and_2_out, not_2_out, b, ieq);
  or or_1 (ogt, and_1_out, igt);
  xnor xnor_1 (xnor_1_out, a, b);
  or or_2 (olt, and_2_out, ilt);
  or or_3 (oeq, xnor_1_out, ieq);
endmodule
