// Logisim project p1.circ as structural Verilog: 3 circuits, main circuit main
module main (
  input  in_1,
  input  in_2,
  input  in_3,
  input  in_4,
  input  in_5,
  input  in_6,
  output P1,
  output P0,
  output P5,
  output P4,
  output P3,
  output P2
);

  wire and_1_out, and_2_out, and_3_out, and_4_out, and_5_out, and_6_out, and_7_out, and_8_out,
       full_adder_2_carry, full_adder_3_carry, full_adder_3_sum, half_adder_1_carry, half_adder_1_sum,
       half_adder_2_carry, half_adder_3_carry;

  and and_1 (and_1_out, in_6, in_5);
  Full_Adder full_adder_1 (.A(full_adder_2_carry), .B(half_adder_1_carry), .C(and_1_out), .SUM(P4), .CARRY(P5));
  and and_2 (and_2_out, in_4, in_5);
  and and_3 (and_3_out, in_6, in_3);
  Half_Adder half_adder_1 (.A(full_adder_3_carry), .B(and_3_out), .SUM(half_adder_1_sum), .CARRY(half_adder_1_carry));
  Full_Adder full_adder_2 (
    .A(half_adder_2_carry), .B(half_adder_1_sum), .C(and_2_out), .SUM(P3), .CARRY(full_adder_2_carry));
  and and_4 (and_4_out, in_4, in_3);
  and and_5 (and_5_out, in_6, in_1);
  and and_6 (and_6_out, in_2, in_5);
  Full_Adder full_adder_3 (
    .A(half_adder_3_carry), .B(and_5_out), .C(and_4_out), .SUM(full_adder_3_sum), .CARRY(full_adder_3_carry));
  Half_Adder half_adder_2 (.A(full_adder_3_sum), .B(and_6_out), .SUM(P2), .CARRY(half_adder_2_carry));
  and and_7 (and_7_out, in_2, in_3);
  and and_8 (and_8_out, in_4, in_1);
  Half_Adder half_adder_3 (.A(and_8_out), .B(and_7_out), .SUM(P1), .CARRY(half_adder_3_carry));
  and and_9 (P0, in_2, in_1);

  // Other names for the same wires on the sheet: X0 = in_2; X1 = in_4; X2 = in_6; Y0 = in_1; Y1 = in_3; Y2 = in_5
endmodule

module Half_Adder (
  input  A,
  input  B,
  output SUM,
  output CARRY
);

  xor xor_1 (SUM, A, B);
  and and_1 (CARRY, B, A);
endmodule

module Full_Adder (
  input  A,
  input  B,
  input  C,
  output SUM,
  output CARRY
);

  wire and_1_out, and_2_out, xor_1_out;

  xor xor_1 (xor_1_out, A, B);
  and and_1 (and_1_out, A, B);
  xor xor_2 (SUM, xor_1_out, C);
  and and_2 (and_2_out, xor_1_out, C);
  or or_1 (CARRY, and_1_out, and_2_out);
endmodule
