// Logisim project p2.circ as structural Verilog: 3 circuits, main circuit main
module main (
  input  [7:0] X,
  input  [7:0] Y,
  output [15:0] out_3
);

  wire and_1_out, and_2_out, and_3_out, and_4_out, and_5_out, and_6_out, and_7_out, and_8_out, and_9_out,
       and_10_out, and_11_out, and_12_out, and_13_out, and_14_out, and_15_out, and_16_out, and_17_out,
       and_18_out, and_19_out, and_20_out, and_21_out, and_22_out, and_23_out, and_24_out, and_25_out,
       and_26_out, and_27_out, and_28_out, and_29_out, and_30_out, and_31_out, and_32_out, and_33_out,
       and_34_out, and_35_out, and_36_out, and_37_out, and_38_out, and_39_out, and_40_out, and_41_out,
       and_42_out, and_43_out, and_44_out, and_45_out, and_46_out, and_47_out, and_48_out, and_49_out,
       and_50_out, and_51_out, and_52_out, and_53_out, and_54_out, and_55_out, and_56_out, and_57_out,
       and_58_out, and_59_out, and_60_out, and_61_out, and_62_out, and_63_out, full_adder_2_carry,
       full_adder_2_sum, full_adder_3_carry, full_adder_4_carry, full_adder_4_sum, full_adder_5_carry,
       full_adder_5_sum, full_adder_6_carry, full_adder_7_carry, full_adder_7_sum, full_adder_8_carry,
       full_adder_8_sum, full_adder_9_carry, full_adder_9_sum, full_adder_10_carry, full_adder_11_carry,
       full_adder_11_sum, full_adder_12_carry, full_adder_12_sum, full_adder_13_carry, full_adder_13_sum,
       full_adder_14_carry, full_adder_14_sum, full_adder_15_carry, full_adder_15_sum, full_adder_16_carry,
       full_adder_17_carry, full_adder_17_sum, full_adder_18_carry, full_adder_18_sum, full_adder_19_carry,
       full_adder_19_sum, full_adder_20_carry, full_adder_20_sum, full_adder_21_carry, full_adder_22_carry,
       full_adder_22_sum, full_adder_23_carry, full_adder_23_sum, full_adder_24_carry, full_adder_24_sum,
       full_adder_25_carry, full_adder_25_sum, full_adder_26_carry, full_adder_26_sum, full_adder_27_carry,
       full_adder_28_carry, full_adder_28_sum, full_adder_29_carry, full_adder_29_sum, full_adder_30_carry,
       full_adder_30_sum, full_adder_31_carry, full_adder_31_sum, full_adder_32_carry, full_adder_32_sum,
       full_adder_33_carry, full_adder_33_sum, full_adder_34_carry, full_adder_34_sum, full_adder_35_carry,
       full_adder_35_sum, full_adder_36_carry, full_adder_36_sum, full_adder_37_carry, full_adder_37_sum,
       full_adder_38_carry, full_adder_38_sum, full_adder_39_carry, full_adder_39_sum, full_adder_40_carry,
       full_adder_40_sum, full_adder_41_carry, full_adder_41_sum, full_adder_42_carry, full_adder_42_sum,
       full_adder_43_carry, full_adder_43_sum, full_adder_44_carry, full_adder_44_sum, full_adder_45_carry,
       full_adder_45_sum, full_adder_46_carry, full_adder_46_sum, full_adder_47_carry, full_adder_47_sum,
       full_adder_48_carry, full_adder_48_sum, half_adder_1_carry, half_adder_1_sum, half_adder_2_carry,
       half_adder_3_carry, half_adder_4_carry, half_adder_5_carry, half_adder_6_carry, half_adder_7_carry,
       half_adder_8_carry;

  and and_1 (and_1_out, X[7], Y[7]);
  and and_2 (and_2_out, X[7], Y[6]);
  Full_adder full_adder_1 (
    .A(full_adder_2_carry), .B(and_1_out), .C(full_adder_3_carry), .CARRY(out_3[15]), .SUM(out_3[14]));
  Full_adder full_adder_2 (
    .A(full_adder_4_carry), .B(and_2_out), .C(full_adder_5_carry), .CARRY(full_adder_2_carry),
    .SUM(full_adder_2_sum));
  and and_3 (and_3_out, X[6], Y[7]);
  Full_adder full_adder_3 (
    .A(full_adder_2_sum), .B(and_3_out), .C(full_adder_6_carry), .CARRY(full_adder_3_carry), .SUM(out_3[13]));
  and and_4 (and_4_out, X[7], Y[5]);
  Full_adder full_adder_4 (
    .A(full_adder_7_carry), .B(and_4_out), .C(full_adder_8_carry), .CARRY(full_adder_4_carry),
    .SUM(full_adder_4_sum));
  and and_5 (and_5_out, X[6], Y[6]);
  and and_6 (and_6_out, X[5], Y[7]);
  and and_7 (and_7_out, X[7], Y[4]);
  and and_8 (and_8_out, X[6], Y[5]);
  and and_9 (and_9_out, X[5], Y[6]);
  Full_adder full_adder_5 (
    .A(full_adder_4_sum), .B(and_5_out), .C(full_adder_9_carry), .CARRY(full_adder_5_carry),
    .SUM(full_adder_5_sum));
  Full_adder full_adder_6 (
    .A(full_adder_5_sum), .B(and_6_out), .C(full_adder_10_carry), .CARRY(full_adder_6_carry), .SUM(out_3[12]));
  and and_10 (and_10_out, X[7], Y[3]);
  Full_adder full_adder_7 (
    .A(full_adder_11_carry), .B(and_7_out), .C(full_adder_12_carry), .CARRY(full_adder_7_carry),
    .SUM(full_adder_7_sum));
  Full_adder full_adder_8 (
    .A(full_adder_7_sum), .B(and_8_out), .C(full_adder_13_carry), .CARRY(full_adder_8_carry),
    .SUM(full_adder_8_sum));
  Full_adder full_adder_9 (
    .A(full_adder_8_sum), .B(and_9_out), .C(full_adder_15_carry), .CARRY(full_adder_9_carry),
    .SUM(full_adder_9_sum));
  and and_11 (and_11_out, X[4], Y[7]);
  Full_adder full_adder_10 (
    .A(full_adder_9_sum), .B(and_11_out), .C(full_adder_16_carry), .CARRY(full_adder_10_carry),
    .SUM(out_3[11]));
  Full_adder full_adder_11 (
    .A(full_adder_14_carry), .B(and_10_out), .C(full_adder_17_carry), .CARRY(full_adder_11_carry),
    .SUM(full_adder_11_sum));
  and and_12 (and_12_out, X[6], Y[4]);
  Full_adder full_adder_12 (
    .A(full_adder_11_sum), .B(and_12_out), .C(full_adder_18_carry), .CARRY(full_adder_12_carry),
    .SUM(full_adder_12_sum));
  and and_13 (and_13_out, X[5], Y[5]);
  Full_adder full_adder_13 (
    .A(full_adder_12_sum), .B(and_13_out), .C(full_adder_19_carry), .CARRY(full_adder_13_carry),
    .SUM(full_adder_13_sum));
  and and_14 (and_14_out, X[4], Y[6]);
  and and_15 (and_15_out, X[3], Y[7]);
  and and_16 (and_16_out, X[7], Y[2]);
  Full_adder full_adder_14 (
    .A(half_adder_1_carry), .B(and_16_out), .C(full_adder_22_carry), .CARRY(full_adder_14_carry),
    .SUM(full_adder_14_sum));
  and and_17 (and_17_out, X[6], Y[3]);
  and and_18 (and_18_out, X[5], Y[4]);
  and and_19 (and_19_out, X[4], Y[5]);
  and and_20 (and_20_out, X[3], Y[6]);
  Full_adder full_adder_15 (
    .A(full_adder_13_sum), .B(and_14_out), .C(full_adder_20_carry), .CARRY(full_adder_15_carry),
    .SUM(full_adder_15_sum));
  and and_21 (and_21_out, X[2], Y[7]);
  Full_adder full_adder_16 (
    .A(full_adder_15_sum), .B(and_15_out), .C(full_adder_21_carry), .CARRY(full_adder_16_carry),
    .SUM(out_3[10]));
  and and_22 (and_22_out, X[7], Y[1]);
  and and_23 (and_23_out, X[6], Y[2]);
  and and_24 (and_24_out, X[5], Y[3]);
  Full_adder full_adder_17 (
    .A(full_adder_14_sum), .B(and_17_out), .C(full_adder_23_carry), .CARRY(full_adder_17_carry),
    .SUM(full_adder_17_sum));
  Full_adder full_adder_18 (
    .A(full_adder_17_sum), .B(and_18_out), .C(full_adder_24_carry), .CARRY(full_adder_18_carry),
    .SUM(full_adder_18_sum));
  Full_adder full_adder_19 (
    .A(full_adder_18_sum), .B(and_19_out), .C(full_adder_25_carry), .CARRY(full_adder_19_carry),
    .SUM(full_adder_19_sum));
  Full_adder full_adder_20 (
    .A(full_adder_19_sum), .B(and_20_out), .C(full_adder_26_carry), .CARRY(full_adder_20_carry),
    .SUM(full_adder_20_sum));
  Full_adder full_adder_21 (
    .A(full_adder_20_sum), .B(and_21_out), .C(full_adder_27_carry), .CARRY(full_adder_21_carry),
    .SUM(out_3[9]));
  Half_adder half_adder_1 (.A(full_adder_28_carry), .B(and_22_out), .CARRY(half_adder_1_carry), .SUM(half_adder_1_sum));
  and and_25 (and_25_out, X[5], Y[2]);
  Full_adder full_adder_22 (
    .A(half_adder_1_sum), .B(and_23_out), .C(full_adder_29_carry), .CARRY(full_adder_22_carry),
    .SUM(full_adder_22_sum));
  Full_adder full_adder_23 (
    .A(full_adder_22_sum), .B(and_24_out), .C(full_adder_30_carry), .CARRY(full_adder_23_carry),
    .SUM(full_adder_23_sum));
  and and_26 (and_26_out, X[4], Y[4]);
  Full_adder full_adder_24 (
    .A(full_adder_23_sum), .B(and_26_out), .C(full_adder_31_carry), .CARRY(full_adder_24_carry),
    .SUM(full_adder_24_sum));
  and and_27 (and_27_out, X[3], Y[5]);
  Full_adder full_adder_25 (
    .A(full_adder_24_sum), .B(and_27_out), .C(full_adder_32_carry), .CARRY(full_adder_25_carry),
    .SUM(full_adder_25_sum));
  and and_28 (and_28_out, X[2], Y[6]);
  Full_adder full_adder_26 (
    .A(full_adder_25_sum), .B(and_28_out), .C(full_adder_33_carry), .CARRY(full_adder_26_carry),
    .SUM(full_adder_26_sum));
  and and_29 (and_29_out, X[1], Y[7]);
  Full_adder full_adder_27 (
    .A(full_adder_26_sum), .B(and_29_out), .C(half_adder_2_carry), .CARRY(full_adder_27_carry), .SUM(out_3[8]));
  and and_30 (and_30_out, X[7], Y[0]);
  and and_31 (and_31_out, X[6], Y[1]);
  Full_adder full_adder_28 (
    .A(and_30_out), .B(and_31_out), .C(full_adder_34_carry), .CARRY(full_adder_28_carry),
    .SUM(full_adder_28_sum));
  Full_adder full_adder_29 (
    .A(full_adder_28_sum), .B(and_25_out), .C(full_adder_35_carry), .CARRY(full_adder_29_carry),
    .SUM(full_adder_29_sum));
  and and_32 (and_32_out, X[4], Y[3]);
  and and_33 (and_33_out, X[3], Y[4]);
  and and_34 (and_34_out, X[2], Y[5]);
  and and_35 (and_35_out, X[1], Y[6]);
  and and_36 (and_36_out, X[0], Y[7]);
  and and_37 (and_37_out, X[5], Y[1]);
  and and_38 (and_38_out, X[4], Y[2]);
  and and_39 (and_39_out, X[3], Y[3]);
  Full_adder full_adder_30 (
    .A(full_adder_29_sum), .B(and_32_out), .C(full_adder_36_carry), .CARRY(full_adder_30_carry),
    .SUM(full_adder_30_sum));
  and and_40 (and_40_out, X[2], Y[4]);
  Full_adder full_adder_31 (
    .A(full_adder_30_sum), .B(and_33_out), .C(full_adder_37_carry), .CARRY(full_adder_31_carry),
    .SUM(full_adder_31_sum));
  and and_41 (and_41_out, X[1], Y[5]);
  Full_adder full_adder_32 (
    .A(full_adder_31_sum), .B(and_34_out), .C(full_adder_38_carry), .CARRY(full_adder_32_carry),
    .SUM(full_adder_32_sum));
  and and_42 (and_42_out, X[0], Y[6]);
  Full_adder full_adder_33 (
    .A(full_adder_32_sum), .B(and_35_out), .C(half_adder_3_carry), .CARRY(full_adder_33_carry),
    .SUM(full_adder_33_sum));
  Half_adder half_adder_2 (.A(full_adder_33_sum), .B(and_36_out), .CARRY(half_adder_2_carry), .SUM(out_3[7]));
  and and_43 (and_43_out, X[6], Y[0]);
  Full_adder full_adder_34 (
    .A(and_43_out), .B(and_37_out), .C(full_adder_39_carry), .CARRY(full_adder_34_carry),
    .SUM(full_adder_34_sum));
  and and_44 (and_44_out, X[3], Y[2]);
  Full_adder full_adder_35 (
    .A(full_adder_34_sum), .B(and_38_out), .C(full_adder_40_carry), .CARRY(full_adder_35_carry),
    .SUM(full_adder_35_sum));
  and and_45 (and_45_out, X[2], Y[3]);
  Full_adder full_adder_36 (
    .A(full_adder_35_sum), .B(and_39_out), .C(full_adder_41_carry), .CARRY(full_adder_36_carry),
    .SUM(full_adder_36_sum));
  Full_adder full_adder_37 (
    .A(full_adder_36_sum), .B(and_40_out), .C(full_adder_42_carry), .CARRY(full_adder_37_carry),
    .SUM(full_adder_37_sum));
  Full_adder full_adder_38 (
    .A(full_adder_37_sum), .B(and_41_out), .C(half_adder_4_carry), .CARRY(full_adder_38_carry),
    .SUM(full_adder_38_sum));
  Half_adder half_adder_3 (.A(full_adder_38_sum), .B(and_42_out), .CARRY(half_adder_3_carry), .SUM(out_3[6]));
  and and_46 (and_46_out, X[5], Y[0]);
  and and_47 (and_47_out, X[4], Y[1]);
  Full_adder full_adder_39 (
    .A(and_46_out), .B(and_47_out), .C(full_adder_43_carry), .CARRY(full_adder_39_carry),
    .SUM(full_adder_39_sum));
  Full_adder full_adder_40 (
    .A(full_adder_39_sum), .B(and_44_out), .C(full_adder_44_carry), .CARRY(full_adder_40_carry),
    .SUM(full_adder_40_sum));
  Full_adder full_adder_41 (
    .A(full_adder_40_sum), .B(and_45_out), .C(full_adder_45_carry), .CARRY(full_adder_41_carry),
    .SUM(full_adder_41_sum));
  and and_48 (and_48_out, X[1], Y[4]);
  Full_adder full_adder_42 (
    .A(full_adder_41_sum), .B(and_48_out), .C(half_adder_5_carry), .CARRY(full_adder_42_carry),
    .SUM(full_adder_42_sum));
  and and_49 (and_49_out, X[0], Y[5]);
  Half_adder half_adder_4 (.A(full_adder_42_sum), .B(and_49_out), .CARRY(half_adder_4_carry), .SUM(out_3[5]));
  and and_50 (and_50_out, X[4], Y[0]);
  and and_51 (and_51_out, X[3], Y[1]);
  Full_adder full_adder_43 (
    .A(and_50_out), .B(and_51_out), .C(full_adder_46_carry), .CARRY(full_adder_43_carry),
    .SUM(full_adder_43_sum));
  and and_52 (and_52_out, X[2], Y[2]);
  Full_adder full_adder_44 (
    .A(full_adder_43_sum), .B(and_52_out), .C(full_adder_47_carry), .CARRY(full_adder_44_carry),
    .SUM(full_adder_44_sum));
  and and_53 (and_53_out, X[1], Y[3]);
  and and_54 (and_54_out, X[0], Y[4]);
  Half_adder half_adder_5 (.A(full_adder_45_sum), .B(and_54_out), .CARRY(half_adder_5_carry), .SUM(out_3[4]));
  and and_55 (and_55_out, X[2], Y[1]);
  and and_56 (and_56_out, X[1], Y[2]);
  and and_57 (and_57_out, X[0], Y[3]);
  Full_adder full_adder_45 (
    .A(full_adder_44_sum), .B(and_53_out), .C(half_adder_6_carry), .CARRY(full_adder_45_carry),
    .SUM(full_adder_45_sum));
  and and_58 (and_58_out, X[3], Y[0]);
  Full_adder full_adder_46 (
    .A(and_58_out), .B(and_55_out), .C(full_adder_48_carry), .CARRY(full_adder_46_carry),
    .SUM(full_adder_46_sum));
  and and_59 (and_59_out, X[0], Y[2]);
  Full_adder full_adder_47 (
    .A(full_adder_46_sum), .B(and_56_out), .C(half_adder_7_carry), .CARRY(full_adder_47_carry),
    .SUM(full_adder_47_sum));
  Half_adder half_adder_6 (.A(full_adder_47_sum), .B(and_57_out), .CARRY(half_adder_6_carry), .SUM(out_3[3]));
  and and_60 (and_60_out, X[2], Y[0]);
  and and_61 (and_61_out, X[1], Y[1]);
  Full_adder full_adder_48 (
    .A(and_60_out), .B(and_61_out), .C(half_adder_8_carry), .CARRY(full_adder_48_carry),
    .SUM(full_adder_48_sum));
  Half_adder half_adder_7 (.A(full_adder_48_sum), .B(and_59_out), .CARRY(half_adder_7_carry), .SUM(out_3[2]));
  and and_62 (and_62_out, X[1], Y[0]);
  and and_63 (and_63_out, X[0], Y[1]);
  Half_adder half_adder_8 (.A(and_62_out), .B(and_63_out), .CARRY(half_adder_8_carry), .SUM(out_3[1]));
  and and_64 (out_3[0], X[0], Y[0]);
endmodule

// FA
module Full_adder (
  input  A,
  input  B,
  input  C,
  output SUM,
  output CARRY
);

  wire and_1_out, and_2_out, xor_1_out;

  xor xor_1 (xor_1_out, A, B);
  and and_1 (and_1_out, xor_1_out, C);
  and and_2 (and_2_out, A, B);
  xor xor_2 (SUM, xor_1_out, C);
  or or_1 (CARRY, and_1_out, and_2_out);
endmodule

// HA
module Half_adder (
  input  A,
  input  B,
  output SUM,
  output CARRY
);

  xor xor_1 (SUM, A, B);
  and and_1 (CARRY, A, B);
endmodule
