// Logisim project p3.circ as structural Verilog: 2 circuits, main circuit main
module main (
  input  a3,
  input  b3,
  input  a2,
  input  b2,
  input  a1,
  input  b1,
  input  a0,
  input  b0,
  input  igt,
  input  ieq,
  input  ilt,
  output a_b,
  output a_b_2,
  output a_b_3
);

  wire n1_bit_comparator_1_oeq, n1_bit_comparator_1_ogt, n1_bit_comparator_1_olt, n1_bit_comparator_2_oeq,
       n1_bit_comparator_2_ogt, n1_bit_comparator_2_olt, n1_bit_comparator_3_oeq, n1_bit_comparator_3_ogt,
       n1_bit_comparator_3_olt;

  _1_bit_comparator u_1_bit_comparator_1 (
    .igt(igt), .ieq(ieq), .ilt(ilt), .a(a3), .b(b3), .ogt(n1_bit_comparator_1_ogt),
    .oeq(n1_bit_comparator_1_oeq), .olt(n1_bit_comparator_1_olt));
  _1_bit_comparator u_1_bit_comparator_2 (
    .igt(n1_bit_comparator_1_ogt), .ieq(n1_bit_comparator_1_oeq), .ilt(n1_bit_comparator_1_olt), .a(a2),
    .b(b2), .ogt(n1_bit_comparator_2_ogt), .oeq(n1_bit_comparator_2_oeq), .olt(n1_bit_comparator_2_olt));
  _1_bit_comparator u_1_bit_comparator_3 (
    .igt(n1_bit_comparator_2_ogt), .ieq(n1_bit_comparator_2_oeq), .ilt(n1_bit_comparator_2_olt), .a(a1),
    .b(b1), .ogt(n1_bit_comparator_3_ogt), .oeq(n1_bit_comparator_3_oeq), .olt(n1_bit_comparator_3_olt));
  _1_bit_comparator u_1_bit_comparator_4 (
    .igt(n1_bit_comparator_3_ogt), .ieq(n1_bit_comparator_3_oeq), .ilt(n1_bit_comparator_3_olt), .a(a0),
    .b(b0), .ogt(a_b), .oeq(a_b_2), .olt(a_b_3));

  // Notes on the sheet:
  //   1BitComparator
  //   4 bit comparator
endmodule

module _1_bit_comparator (
  input  a,
  input  b,
  input  igt,
  input  ieq,
  input  ilt,
  output ogt,
  output oeq,
  output olt
);

  wire and_1_out, and_2_out, not_1_out, not_2_out, xnor_1_out;

  not not_1 (not_1_out, b);
  not not_2 (not_2_out, a);
  and and_1 (and_1_out, a, not_1_out, ieq);
  and and_2 (and_2_out, not_2_out, b, ieq);
  or or_1 (ogt, and_1_out, igt);
  xnor xnor_1 (xnor_1_out, a, b);
  or or_2 (olt, and_2_out, ilt);
  and and_3 (oeq, xnor_1_out, ieq);

  // Notes on the sheet:
  //   =igt + a . b' . ieq
  //   =ieq . (a^b)'
  //   = ilt + a' . b . ieq
endmodule
