// Logisim project p4.circ as structural Verilog: 3 circuits, main circuit main
module main (
  input  [7:0] a,
  input  [7:0] b,
  input  igt,
  input  ieq,
  input  ilt,
  output ogt,
  output oeq,
  output [7:0] minimum_a_b
);

  wire n4_bit_comparator_1_a_b, n4_bit_comparator_1_a_b_2, n4_bit_comparator_1_a_b_3;
  wire [7:0] and_1_out, and_2_out, not_1_out;
  wire [7:7] n4_bit_comparator_2_a_b_3;

  _4_bit_comparator u_4_bit_comparator_1 (
    .igt(igt), .ieq(ieq), .ilt(ilt), .a3(a[7]), .b3(b[7]), .a2(a[6]), .b2(b[6]), .a1(a[5]), .b1(b[5]),
    .a0(a[4]), .b0(b[4]), .a_b(n4_bit_comparator_1_a_b), .a_b_2(n4_bit_comparator_1_a_b_2),
    .a_b_3(n4_bit_comparator_1_a_b_3));
  _4_bit_comparator u_4_bit_comparator_2 (
    .igt(n4_bit_comparator_1_a_b), .ieq(n4_bit_comparator_1_a_b_2), .ilt(n4_bit_comparator_1_a_b_3),
    .a3(a[3]), .b3(b[3]), .a2(a[2]), .b2(b[2]), .a1(a[1]), .b1(b[1]), .a0(a[0]), .b0(b[0]), .a_b(ogt),
    .a_b_2(oeq), .a_b_3(n4_bit_comparator_2_a_b_3[7]));
  assign not_1_out = ~{8{n4_bit_comparator_2_a_b_3[7]}};  // NOT_Gate not_1, 8 bits wide
  assign and_1_out = {8{n4_bit_comparator_2_a_b_3[7]}} & a;  // AND_Gate and_1, 8 bits wide
  assign minimum_a_b = and_1_out | and_2_out;  // OR_Gate or_1, 8 bits wide
  assign and_2_out = not_1_out & b;  // AND_Gate and_2, 8 bits wide
endmodule

// 4 bit comparator
module _4_bit_comparator (
  input  a3,
  input  b3,
  input  a2,
  input  b2,
  input  a1,
  input  b1,
  input  a0,
  input  b0,
  input  igt,
  input  ieq,
  input  ilt,
  output a_b,
  output a_b_2,
  output a_b_3
);

  wire n1_bit_comparator_1_oeq, n1_bit_comparator_1_ogt, n1_bit_comparator_1_olt, n1_bit_comparator_2_oeq,
       n1_bit_comparator_2_ogt, n1_bit_comparator_2_olt, n1_bit_comparator_3_oeq, n1_bit_comparator_3_ogt,
       n1_bit_comparator_3_olt;

  p3_1_bit_comparator u_1_bit_comparator_1 (
    .igt(igt), .ieq(ieq), .ilt(ilt), .a(a3), .b(b3), .ogt(n1_bit_comparator_1_ogt),
    .oeq(n1_bit_comparator_1_oeq), .olt(n1_bit_comparator_1_olt));
  p3_1_bit_comparator u_1_bit_comparator_2 (
    .igt(n1_bit_comparator_1_ogt), .ieq(n1_bit_comparator_1_oeq), .ilt(n1_bit_comparator_1_olt), .a(a2),
    .b(b2), .ogt(n1_bit_comparator_2_ogt), .oeq(n1_bit_comparator_2_oeq), .olt(n1_bit_comparator_2_olt));
  p3_1_bit_comparator u_1_bit_comparator_3 (
    .igt(n1_bit_comparator_2_ogt), .ieq(n1_bit_comparator_2_oeq), .ilt(n1_bit_comparator_2_olt), .a(a1),
    .b(b1), .ogt(n1_bit_comparator_3_ogt), .oeq(n1_bit_comparator_3_oeq), .olt(n1_bit_comparator_3_olt));
  p3_1_bit_comparator u_1_bit_comparator_4 (
    .igt(n1_bit_comparator_3_ogt), .ieq(n1_bit_comparator_3_oeq), .ilt(n1_bit_comparator_3_olt), .a(a0),
    .b(b0), .ogt(a_b), .oeq(a_b_2), .olt(a_b_3));
endmodule

module _1_bit_comparator (
  input  a,
  input  b,
  input  igt,
  input  ieq,
  input  ilt,
  output ogt,
  output oeq,
  output olt
);

  wire and_1_out, and_2_out, not_1_out, not_2_out, xnor_1_out;

  not not_1 (not_1_out, b);
  not not_2 (not_2_out, a);
  and and_1 (and_1_out, a, not_1_out, ieq);
  and and_2 (and_2_out, not_2_out, b, ieq);
  or or_1 (ogt, and_1_out, igt);
  xnor xnor_1 (xnor_1_out, a, b);
  or or_2 (olt, and_2_out, ilt);
  and and_3 (oeq, xnor_1_out, ieq);
endmodule
