// Logisim project p1.circ as structural Verilog: 11 circuits, main circuit main
// A/S
module _8_bit_adder_subtractor (
  input  Addition_Substration,
  input  [7:0] B,
  input  [7:0] A,
  output [7:0] out_4
);

  wire n4bit_adder_2_c_out, xor_1_out, xor_2_out, xor_3_out, xor_4_out, xor_5_out, xor_6_out, xor_7_out,
       xor_8_out;

  xor xor_1 (xor_1_out, B[7], Addition_Substration);
  xor xor_2 (xor_2_out, B[6], Addition_Substration);
  xor xor_3 (xor_3_out, B[5], Addition_Substration);
  _4bit_adder u_4bit_adder_1 (
    .b3(A[7]), .a3(xor_1_out), .b2(A[6]), .a2(xor_2_out), .b1(A[5]), .a1(xor_3_out), .b0(A[4]),
    .a0(xor_4_out), .s3(out_4[7]), .s2(out_4[6]), .s1(out_4[5]), .s0(out_4[4]), .c_in(n4bit_adder_2_c_out));  // open: c_out
  xor xor_4 (xor_4_out, B[4], Addition_Substration);
  xor xor_5 (xor_5_out, B[3], Addition_Substration);
  xor xor_6 (xor_6_out, B[2], Addition_Substration);
  xor xor_7 (xor_7_out, B[1], Addition_Substration);
  _4bit_adder u_4bit_adder_2 (
    .c_out(n4bit_adder_2_c_out), .b3(A[3]), .a3(xor_5_out), .b2(A[2]), .a2(xor_6_out), .b1(A[1]),
    .a1(xor_7_out), .b0(A[0]), .a0(xor_8_out), .s3(out_4[3]), .s2(out_4[2]), .s1(out_4[1]), .s0(out_4[0]),
    .c_in(Addition_Substration));
  xor xor_8 (xor_8_out, B[0], Addition_Substration);
endmodule

module main (
  input  [7:0] A,
  input  [7:0] B,
  input  [2:0] in_3,
  output [7:0] Output
);

  wire [7:0] and_1_out_3, is_a_b_1_out_3, maximum_1_maximum_a_b, minimum_1_maximum_a_b,
       n8_bit_adder_subtractor_1_out_4, n8_bit_adder_subtractor_2_out_4, or_1_out_3, xor_1_out_3;

  _8_bit_adder_subtractor u_8_bit_adder_subtractor_1 (
    .B(B), .A(A), .Addition_Substration(1'b0), .out_4(n8_bit_adder_subtractor_1_out_4));
  _8_bit_adder_subtractor u_8_bit_adder_subtractor_2 (
    .B(B), .A(A), .Addition_Substration(1'b1), .out_4(n8_bit_adder_subtractor_2_out_4));
  AND and_1 (.A(A), .B(B), .out_3(and_1_out_3));
  OR or_1 (.A(A), .B(B), .out_3(or_1_out_3));
  XOR xor_1 (.A(A), .B(B), .out_3(xor_1_out_3));
  Maximum maximum_1 (.A(A), .B(B), .Maximum_A_B(maximum_1_maximum_a_b));
  Minimum minimum_1 (.A(A), .B(B), .Maximum_A_B(minimum_1_maximum_a_b));
  IS_A_B is_a_b_1 (.A(A), .B(B), .out_3(is_a_b_1_out_3));
  Multiplexer #(.select(3), .width(8)) multiplexer_1 (
    .in0(n8_bit_adder_subtractor_1_out_4), .in1(n8_bit_adder_subtractor_2_out_4), .in2(and_1_out_3),
    .in3(or_1_out_3), .in4(xor_1_out_3), .in5(maximum_1_maximum_a_b), .in6(minimum_1_maximum_a_b),
    .in7(is_a_b_1_out_3), .out(Output), .sel(in_3));  // open: en
endmodule

module AND (
  input  [7:0] A,
  input  [7:0] B,
  output [7:0] out_3
);

  assign out_3 = A & B;  // AND_Gate and_1, 8 bits wide
endmodule

module OR (
  input  [7:0] A,
  input  [7:0] B,
  output [7:0] out_3
);

  assign out_3 = A | B;  // OR_Gate or_1, 8 bits wide
endmodule

module XOR (
  input  [7:0] A,
  input  [7:0] B,
  output [7:0] out_3
);

  assign out_3 = A ^ B;  // XOR_Gate xor_1, 8 bits wide
endmodule

// MAX
module Maximum (
  input  [7:0] A,
  input  [7:0] B,
  output [7:0] Maximum_A_B
);

  wire n4_bit_comparator_1_a_b, n4_bit_comparator_1_a_b_2, n4_bit_comparator_1_a_b_3, n4_bit_comparator_2_a_b;

  _4_bit_comparator u_4_bit_comparator_1 (
    .igt(1'b0), .ieq(1'b1), .ilt(1'b0), .a3(A[7]), .b3(B[7]), .a2(A[6]), .b2(B[6]), .a1(A[5]), .b1(B[5]),
    .a0(A[4]), .b0(B[4]), .a_b(n4_bit_comparator_1_a_b), .a_b_2(n4_bit_comparator_1_a_b_2),
    .a_b_3(n4_bit_comparator_1_a_b_3));
  _4_bit_comparator u_4_bit_comparator_2 (
    .igt(n4_bit_comparator_1_a_b), .ieq(n4_bit_comparator_1_a_b_2), .ilt(n4_bit_comparator_1_a_b_3),
    .a3(A[3]), .b3(B[3]), .a2(A[2]), .b2(B[2]), .a1(A[1]), .b1(B[1]), .a0(A[0]), .b0(B[0]),
    .a_b(n4_bit_comparator_2_a_b));  // open: a_b_2, a_b_3
  Multiplexer #(.width(8)) multiplexer_1 (
    .in0(B), .in1(A), .out(Maximum_A_B), .sel(n4_bit_comparator_2_a_b));  // open: en
endmodule

// MIN
module Minimum (
  input  [7:0] A,
  input  [7:0] B,
  output [7:0] Maximum_A_B
);

  wire n4_bit_comparator_1_a_b, n4_bit_comparator_1_a_b_2, n4_bit_comparator_1_a_b_3,
       n4_bit_comparator_2_a_b_3;

  _4_bit_comparator u_4_bit_comparator_1 (
    .igt(1'b0), .ieq(1'b1), .ilt(1'b0), .a3(A[7]), .b3(B[7]), .a2(A[6]), .b2(B[6]), .a1(A[5]), .b1(B[5]),
    .a0(A[4]), .b0(B[4]), .a_b(n4_bit_comparator_1_a_b), .a_b_2(n4_bit_comparator_1_a_b_2),
    .a_b_3(n4_bit_comparator_1_a_b_3));
  _4_bit_comparator u_4_bit_comparator_2 (
    .igt(n4_bit_comparator_1_a_b), .ieq(n4_bit_comparator_1_a_b_2), .ilt(n4_bit_comparator_1_a_b_3),
    .a3(A[3]), .b3(B[3]), .a2(A[2]), .b2(B[2]), .a1(A[1]), .b1(B[1]), .a0(A[0]), .b0(B[0]),
    .a_b_3(n4_bit_comparator_2_a_b_3));  // open: a_b, a_b_2
  Multiplexer #(.width(8)) multiplexer_1 (
    .in0(B), .in1(A), .out(Maximum_A_B), .sel(n4_bit_comparator_2_a_b_3));  // open: en
endmodule

// A>B
module IS_A_B (
  input  [7:0] A,
  input  [7:0] B,
  output [7:0] out_3
);

  wire n4_bit_comparator_1_a_b, n4_bit_comparator_1_a_b_2, n4_bit_comparator_1_a_b_3;

  _4_bit_comparator u_4_bit_comparator_1 (
    .igt(1'b0), .ieq(1'b1), .ilt(1'b0), .a3(A[7]), .b3(B[7]), .a2(A[6]), .b2(B[6]), .a1(A[5]), .b1(B[5]),
    .a0(A[4]), .b0(B[4]), .a_b(n4_bit_comparator_1_a_b), .a_b_2(n4_bit_comparator_1_a_b_2),
    .a_b_3(n4_bit_comparator_1_a_b_3));
  _4_bit_comparator u_4_bit_comparator_2 (
    .igt(n4_bit_comparator_1_a_b), .ieq(n4_bit_comparator_1_a_b_2), .ilt(n4_bit_comparator_1_a_b_3),
    .a3(A[3]), .b3(B[3]), .a2(A[2]), .b2(B[2]), .a1(A[1]), .b1(B[1]), .a0(A[0]), .b0(B[0]), .a_b(out_3[0]));  // open: a_b_2, a_b_3

  assign out_3[7:1] = {7{1'b0}};
endmodule

module _4bit_adder (
  input  b0,
  input  a0,
  input  b3,
  input  a3,
  input  b2,
  input  a2,
  input  b1,
  input  a1,
  input  c_in,
  output s3,
  output s2,
  output s1,
  output s0,
  output c_out
);

  wire adder_2_cout, adder_3_cout, adder_4_cout;

  Adder #(.width(1)) adder_1 (.a(a3), .b(b3), .out(s3), .cin(adder_2_cout), .cout(c_out));
  Adder #(.width(1)) adder_2 (.a(a2), .b(b2), .out(s2), .cin(adder_3_cout), .cout(adder_2_cout));
  Adder #(.width(1)) adder_3 (.a(a1), .b(b1), .out(s1), .cin(adder_4_cout), .cout(adder_3_cout));
  Adder #(.width(1)) adder_4 (.a(a0), .b(b0), .out(s0), .cin(c_in), .cout(adder_4_cout));
endmodule

module _4_bit_comparator (
  input  a3,
  input  b3,
  input  a2,
  input  b2,
  input  a1,
  input  b1,
  input  a0,
  input  b0,
  input  igt,
  input  ieq,
  input  ilt,
  output a_b,
  output a_b_2,
  output a_b_3
);

  wire n1_bit_comparator_1_oeq, n1_bit_comparator_1_ogt, n1_bit_comparator_1_olt, n1_bit_comparator_2_oeq,
       n1_bit_comparator_2_ogt, n1_bit_comparator_2_olt, n1_bit_comparator_3_oeq, n1_bit_comparator_3_ogt,
       n1_bit_comparator_3_olt;

  _1_bit_comparator u_1_bit_comparator_1 (
    .igt(igt), .ieq(ieq), .ilt(ilt), .a(a3), .b(b3), .ogt(n1_bit_comparator_1_ogt),
    .oeq(n1_bit_comparator_1_oeq), .olt(n1_bit_comparator_1_olt));
  _1_bit_comparator u_1_bit_comparator_2 (
    .igt(n1_bit_comparator_1_ogt), .ieq(n1_bit_comparator_1_oeq), .ilt(n1_bit_comparator_1_olt), .a(a2),
    .b(b2), .ogt(n1_bit_comparator_2_ogt), .oeq(n1_bit_comparator_2_oeq), .olt(n1_bit_comparator_2_olt));
  _1_bit_comparator u_1_bit_comparator_3 (
    .igt(n1_bit_comparator_2_ogt), .ieq(n1_bit_comparator_2_oeq), .ilt(n1_bit_comparator_2_olt), .a(a1),
    .b(b1), .ogt(n1_bit_comparator_3_ogt), .oeq(n1_bit_comparator_3_oeq), .olt(n1_bit_comparator_3_olt));
  _1_bit_comparator u_1_bit_comparator_4 (
    .igt(n1_bit_comparator_3_ogt), .ieq(n1_bit_comparator_3_oeq), .ilt(n1_bit_comparator_3_olt), .a(a0),
    .b(b0), .ogt(a_b), .oeq(a_b_2), .olt(a_b_3));
endmodule

module _1_bit_comparator (
  input  a,
  input  b,
  input  igt,
  input  ieq,
  input  ilt,
  output ogt,
  output oeq,
  output olt
);

  wire and_1_out, and_2_out, not_1_out, not_2_out, xnor_1_out;

  not not_1 (not_1_out, b);
  not not_2 (not_2_out, a);
  and and_1 (and_1_out, a, not_1_out, ieq);
  and and_2 (and_2_out, not_2_out, b, ieq);
  or or_1 (ogt, and_1_out, igt);
  xnor xnor_1 (xnor_1_out, a, b);
  or or_2 (olt, and_2_out, ilt);
  and and_3 (oeq, xnor_1_out, ieq);
endmodule
