// Logisim project Q0.circ as structural Verilog: 1 circuit, main circuit main
module main (
  input  in_1,
  input  in_2,
  input  in_3,
  input  in_4,
  input  Preset,
  input  Preset_2,
  input  Enable,
  input  Enable_2,
  input  Clear,
  input  Clear_2,
  input  in_11,
  input  in_12,
  input  Preset_3,
  input  Preset_4,
  input  Enable_3,
  input  Enable_4,
  input  Clear_3,
  input  Clear_4
);

  wire Clock_2_out, Clock_3_out, Clock_4_out, Clock_out, d_ff_1_q, j_k_ff_1_q, s_r_ff_1_q, t_ff_1_q;

  Clock Clock (.out(Clock_out));
  J_K_Flip_Flop j_k_ff_1 (
    .J(in_2), .clk(Clock_out), .K(in_4), .Q(j_k_ff_1_q), .preset(Preset_2), .en(Enable_2), .reset(Clear_2));  // open: Qn
  LED led_1 (.in(j_k_ff_1_q));
  Clock Clock_2 (.out(Clock_2_out));
  T_Flip_Flop t_ff_1 (
    .clk(Clock_2_out), .T(in_11), .Q(t_ff_1_q), .preset(Preset_3), .reset(Clear_3), .en(Enable_3));  // open: Qn
  LED led_2 (.in(t_ff_1_q));
  Clock Clock_3 (.out(Clock_3_out));
  S_R_Flip_Flop s_r_ff_1 (
    .S(in_1), .clk(Clock_3_out), .R(in_3), .Q(s_r_ff_1_q), .preset(Preset), .reset(Clear), .en(Enable));  // open: Qn
  LED led_3 (.in(s_r_ff_1_q));
  Clock Clock_4 (.out(Clock_4_out));
  D_Flip_Flop d_ff_1 (
    .clk(Clock_4_out), .D(in_12), .Q(d_ff_1_q), .preset(Preset_4), .en(Enable_4), .reset(Clear_4));  // open: Qn
  LED led_4 (.in(d_ff_1_q));

  // Notes on the sheet:
  //   J-K Flip Flop
  //   T Flip Flop
  //   S-R Flip Flop
  //   D Flip Flop
endmodule
