// Logisim project Q1.circ as structural Verilog: 1 circuit, main circuit main
module main (
  input  Enable,
  input  Input
);

  wire Clock_out;
  wire [3:0] d_ff_4_q, d_ff_8_q;

  Clock Clock (.out(Clock_out));
  D_Flip_Flop d_ff_1 (.clk(Clock_out), .D(d_ff_4_q[2]), .Q(d_ff_4_q[3]), .en(Enable));  // open: Qn, preset, reset
  D_Flip_Flop d_ff_2 (.clk(Clock_out), .D(d_ff_4_q[1]), .Q(d_ff_4_q[2]), .en(Enable));  // open: Qn, preset, reset
  D_Flip_Flop d_ff_3 (.clk(Clock_out), .D(d_ff_4_q[0]), .Q(d_ff_4_q[1]), .en(Enable));  // open: Qn, preset, reset
  D_Flip_Flop d_ff_4 (.clk(Clock_out), .D(d_ff_8_q[3]), .Q(d_ff_4_q[0]), .en(Enable));  // open: Qn, preset, reset
  D_Flip_Flop d_ff_5 (.clk(Clock_out), .D(d_ff_8_q[2]), .Q(d_ff_8_q[3]), .en(Enable));  // open: Qn, preset, reset
  D_Flip_Flop d_ff_6 (.clk(Clock_out), .D(d_ff_8_q[1]), .Q(d_ff_8_q[2]), .en(Enable));  // open: Qn, preset, reset
  D_Flip_Flop d_ff_7 (.clk(Clock_out), .D(d_ff_8_q[0]), .Q(d_ff_8_q[1]), .en(Enable));  // open: Qn, preset, reset
  D_Flip_Flop d_ff_8 (.clk(Clock_out), .D(Input), .Q(d_ff_8_q[0]), .en(Enable));  // open: Qn, preset, reset
  LED bit_8 (.in(d_ff_4_q[3]));
  LED bit_7 (.in(d_ff_4_q[2]));
  LED bit_6 (.in(d_ff_4_q[1]));
  LED bit_5 (.in(d_ff_4_q[0]));
  LED bit_4 (.in(d_ff_8_q[3]));
  LED bit_3 (.in(d_ff_8_q[2]));
  LED bit_2 (.in(d_ff_8_q[1]));
  LED bit_1 (.in(d_ff_8_q[0]));
  Hex_Digit_Display hex_digit_display_1 (.value(d_ff_4_q));  // open: dp
  Hex_Digit_Display hex_digit_display_2 (.value(d_ff_8_q));  // open: dp

  // Notes on the sheet:
  //   8 bit shift register
  //   Output in Hexadecimal
endmodule
