// Logisim project Q3.circ as structural Verilog: 1 circuit, main circuit main
module main (
  input  T,
  input  Reset
);

  wire Clock_out;
  wire [1:0] t_ff_5_q;
  wire [3:0] t_ff_1_q;

  Clock Clock (.out(Clock_out));
  Hex_Digit_Display hex_digit_display_1 (.value({2'b00, t_ff_5_q}));  // open: dp
  Hex_Digit_Display hex_digit_display_2 (.value(t_ff_1_q));  // open: dp
  T_Flip_Flop #(.trigger("falling")) t_ff_1 (
    .clk(Clock_out), .T(T), .Q(t_ff_1_q[0]), .reset(Reset));  // open: Qn, preset, en
  LED led_1 (.in(t_ff_5_q[1]));
  T_Flip_Flop #(.trigger("falling")) t_ff_2 (
    .clk(t_ff_1_q[0]), .T(T), .Q(t_ff_1_q[1]), .reset(Reset));  // open: Qn, preset, en
  LED led_2 (.in(t_ff_5_q[0]));
  T_Flip_Flop #(.trigger("falling")) t_ff_3 (
    .clk(t_ff_1_q[1]), .T(T), .Q(t_ff_1_q[2]), .reset(Reset));  // open: Qn, preset, en
  LED led_3 (.in(t_ff_1_q[3]));
  T_Flip_Flop #(.trigger("falling")) t_ff_4 (
    .clk(t_ff_1_q[2]), .T(T), .Q(t_ff_1_q[3]), .reset(Reset));  // open: Qn, preset, en
  LED led_4 (.in(t_ff_1_q[2]));
  T_Flip_Flop #(.trigger("falling")) t_ff_5 (
    .clk(t_ff_1_q[3]), .T(T), .Q(t_ff_5_q[0]), .reset(Reset));  // open: Qn, preset, en
  LED led_5 (.in(t_ff_1_q[1]));
  T_Flip_Flop #(.trigger("falling")) t_ff_6 (
    .clk(t_ff_5_q[0]), .T(T), .Q(t_ff_5_q[1]), .reset(Reset));  // open: Qn, preset, en
  LED led_6 (.in(t_ff_1_q[0]));

  // Notes on the sheet:
  //   Output in Hexadecimal 
  //   Bit 1 (LSB)
  //   Bit 6 (MSB)
  //   Bit 2
  //   Bit 5
  //   6 bit counter using T flip flops
  //   Bit 3
  //   Bit 4
  //   Bit 4
  //   Bit 5
  //   Bit 3
  //   Bit 2
  //   Bit 6 (MSB)
  //   Bit 1 (LSB)
endmodule
