// Logisim project Q4.circ as structural Verilog: 1 circuit, main circuit main
module main (
  input  I7,
  input  I6,
  input  I5,
  input  I4,
  input  I3,
  input  I2,
  input  I1,
  input  I0,
  input  shr_in,
  input  [1:0] s1_s0,
  output Q7,
  output Q6,
  output Q5,
  output Q4,
  output Q3,
  output Q2,
  output Q1,
  output Q0
);

  wire Clock_out, multiplexer_1_out, multiplexer_2_out, multiplexer_3_out, multiplexer_4_out,
       multiplexer_5_out, multiplexer_6_out, multiplexer_7_out, multiplexer_8_out;

  Clock Clock (.out(Clock_out));
  Multiplexer #(.select(2), .enable("false")) multiplexer_1 (
    .in0(Q7), .in1(I7), .in2(shr_in), .in3(1'b0), .out(multiplexer_1_out), .sel(s1_s0));
  D_Flip_Flop d_ff_1 (.clk(Clock_out), .D(multiplexer_1_out), .Q(Q7));  // open: Qn, preset, en, reset
  Multiplexer #(.select(2), .enable("false")) multiplexer_2 (
    .in0(Q6), .in1(I6), .in2(Q7), .in3(1'b0), .out(multiplexer_2_out), .sel(s1_s0));
  D_Flip_Flop d_ff_2 (.clk(Clock_out), .D(multiplexer_2_out), .Q(Q6));  // open: Qn, preset, en, reset
  Multiplexer #(.select(2), .enable("false")) multiplexer_3 (
    .in0(Q5), .in1(I5), .in2(Q6), .in3(1'b0), .out(multiplexer_3_out), .sel(s1_s0));
  D_Flip_Flop d_ff_3 (.clk(Clock_out), .D(multiplexer_3_out), .Q(Q5));  // open: Qn, preset, en, reset
  Multiplexer #(.select(2), .enable("false")) multiplexer_4 (
    .in0(Q4), .in1(I4), .in2(Q5), .in3(1'b0), .out(multiplexer_4_out), .sel(s1_s0));
  Multiplexer #(.select(2), .enable("false")) multiplexer_5 (
    .in0(Q3), .in1(I3), .in2(Q4), .in3(1'b0), .out(multiplexer_5_out), .sel(s1_s0));
  D_Flip_Flop d_ff_4 (.clk(Clock_out), .D(multiplexer_4_out), .Q(Q4));  // open: Qn, preset, en, reset
  D_Flip_Flop d_ff_5 (.clk(Clock_out), .D(multiplexer_5_out), .Q(Q3));  // open: Qn, preset, en, reset
  Multiplexer #(.select(2), .enable("false")) multiplexer_6 (
    .in0(Q2), .in1(I2), .in2(Q3), .in3(1'b0), .out(multiplexer_6_out), .sel(s1_s0));
  D_Flip_Flop d_ff_6 (.clk(Clock_out), .D(multiplexer_6_out), .Q(Q2));  // open: Qn, preset, en, reset
  Multiplexer #(.select(2), .enable("false")) multiplexer_7 (
    .in0(Q1), .in1(I1), .in2(Q2), .in3(1'b0), .out(multiplexer_7_out), .sel(s1_s0));
  D_Flip_Flop d_ff_7 (.clk(Clock_out), .D(multiplexer_7_out), .Q(Q1));  // open: Qn, preset, en, reset
  Multiplexer #(.select(2), .enable("false")) multiplexer_8 (
    .in0(Q0), .in1(I0), .in2(Q1), .in3(1'b0), .out(multiplexer_8_out), .sel(s1_s0));
  D_Flip_Flop d_ff_8 (.clk(Clock_out), .D(multiplexer_8_out), .Q(Q0));  // open: Qn, preset, en, reset

  // Notes on the sheet:
  //   s1   s0    Operation
  //   0    0   Maintain present value
  //   0   1   Parallel load
  //   1   0   Shift right
  //   1   1   unused-load zeros
  //   8 Bit Multi-function Shift Register
endmodule
