// Logisim project Q1.circ as structural Verilog: 1 circuit, main circuit main
module main (
  input  [15:0] Input_Terminal__16_Bit,
  input  [3:0] Writing_Address,
  input  [3:0] Reading_Address_1,
  input  [3:0] Reading_Address_2,
  input  Write_Enable,
  input  Read_Enable,
  input  Clear,
  output [15:0] Read_Value_1,
  output [15:0] Read_Value_2
);

  wire and_1_out, and_2_out, and_3_out, and_4_out, and_5_out, and_6_out, and_7_out, and_8_out, and_9_out,
       and_10_out, and_11_out, and_12_out, and_13_out, and_14_out, and_15_out, and_16_out, Clock_out,
       decoder_1_out0, decoder_1_out1, decoder_1_out2, decoder_1_out3, decoder_1_out4, decoder_1_out5,
       decoder_1_out6, decoder_1_out7, decoder_1_out8, decoder_1_out9, decoder_1_out10, decoder_1_out11,
       decoder_1_out12, decoder_1_out13, decoder_1_out14, decoder_1_out15;
  wire [15:0] register_1_q, register_2_q, register_3_q, register_4_q, register_5_q, register_6_q,
       register_7_q, register_8_q, register_9_q, register_10_q, register_11_q, register_12_q, register_13_q,
       register_14_q, register_15_q, register_16_q;

  Clock Clock (.out(Clock_out));
  Decoder #(.select(4)) decoder_1 (
    .out0(decoder_1_out0), .out1(decoder_1_out1), .out2(decoder_1_out2), .out3(decoder_1_out3),
    .out4(decoder_1_out4), .out5(decoder_1_out5), .out6(decoder_1_out6), .out7(decoder_1_out7),
    .out8(decoder_1_out8), .out9(decoder_1_out9), .out10(decoder_1_out10), .out11(decoder_1_out11),
    .out12(decoder_1_out12), .out13(decoder_1_out13), .out14(decoder_1_out14), .out15(decoder_1_out15),
    .sel(Writing_Address));  // open: en
  and and_1 (and_1_out, decoder_1_out0, Write_Enable);
  and and_2 (and_2_out, decoder_1_out1, Write_Enable);
  and and_3 (and_3_out, decoder_1_out2, Write_Enable);
  and and_4 (and_4_out, decoder_1_out3, Write_Enable);
  and and_5 (and_5_out, decoder_1_out4, Write_Enable);
  and and_6 (and_6_out, decoder_1_out5, Write_Enable);
  and and_7 (and_7_out, decoder_1_out6, Write_Enable);
  and and_8 (and_8_out, decoder_1_out7, Write_Enable);
  and and_9 (and_9_out, Write_Enable, decoder_1_out8);
  and and_10 (and_10_out, Write_Enable, decoder_1_out9);
  and and_11 (and_11_out, Write_Enable, decoder_1_out10);
  and and_12 (and_12_out, Write_Enable, decoder_1_out11);
  and and_13 (and_13_out, Write_Enable, decoder_1_out12);
  and and_14 (and_14_out, Write_Enable, decoder_1_out13);
  and and_15 (and_15_out, Write_Enable, decoder_1_out14);
  and and_16 (and_16_out, Write_Enable, decoder_1_out15);
  Register #(.width(16)) register_1 (
    .D(Input_Terminal__16_Bit), .en(and_1_out), .Q(register_1_q), .clk(Clock_out), .clr(Clear));
  Register #(.width(16)) register_2 (
    .D(Input_Terminal__16_Bit), .en(and_2_out), .Q(register_2_q), .clk(Clock_out), .clr(Clear));
  Register #(.width(16)) register_3 (
    .D(Input_Terminal__16_Bit), .en(and_3_out), .Q(register_3_q), .clk(Clock_out), .clr(Clear));
  Register #(.width(16)) register_4 (
    .D(Input_Terminal__16_Bit), .en(and_4_out), .Q(register_4_q), .clk(Clock_out), .clr(Clear));
  Register #(.width(16)) register_5 (
    .D(Input_Terminal__16_Bit), .en(and_5_out), .Q(register_5_q), .clk(Clock_out), .clr(Clear));
  Register #(.width(16)) register_6 (
    .D(Input_Terminal__16_Bit), .en(and_6_out), .Q(register_6_q), .clk(Clock_out), .clr(Clear));
  Register #(.width(16)) register_7 (
    .D(Input_Terminal__16_Bit), .en(and_7_out), .Q(register_7_q), .clk(Clock_out), .clr(Clear));
  Register #(.width(16)) register_8 (
    .D(Input_Terminal__16_Bit), .en(and_8_out), .Q(register_8_q), .clk(Clock_out), .clr(Clear));
  Register #(.width(16)) register_9 (
    .D(Input_Terminal__16_Bit), .en(and_9_out), .Q(register_9_q), .clk(Clock_out), .clr(Clear));
  Register #(.width(16)) register_10 (
    .D(Input_Terminal__16_Bit), .en(and_10_out), .Q(register_10_q), .clk(Clock_out), .clr(Clear));
  Register #(.width(16)) register_11 (
    .D(Input_Terminal__16_Bit), .en(and_11_out), .Q(register_11_q), .clk(Clock_out), .clr(Clear));
  Register #(.width(16)) register_12 (
    .D(Input_Terminal__16_Bit), .en(and_12_out), .Q(register_12_q), .clk(Clock_out), .clr(Clear));
  Register #(.width(16)) register_13 (
    .D(Input_Terminal__16_Bit), .en(and_13_out), .Q(register_13_q), .clk(Clock_out), .clr(Clear));
  Register #(.width(16)) register_14 (
    .D(Input_Terminal__16_Bit), .en(and_14_out), .Q(register_14_q), .clk(Clock_out), .clr(Clear));
  Register #(.width(16)) register_15 (
    .D(Input_Terminal__16_Bit), .en(and_15_out), .Q(register_15_q), .clk(Clock_out), .clr(Clear));
  Register #(.width(16)) register_16 (
    .D(Input_Terminal__16_Bit), .en(and_16_out), .Q(register_16_q), .clk(Clock_out), .clr(Clear));
  Multiplexer #(.select(4), .width(16)) multiplexer_1 (
    .in0(register_1_q), .in1(register_2_q), .in2(register_3_q), .in3(register_4_q), .in4(register_5_q),
    .in5(register_6_q), .in6(register_7_q), .in7(register_8_q), .in8(register_9_q), .in9(register_10_q),
    .in10(register_11_q), .in11(register_12_q), .in12(register_13_q), .in13(register_14_q),
    .in14(register_15_q), .in15(register_16_q), .out(Read_Value_1), .sel(Reading_Address_1), .en(Read_Enable));
  Multiplexer #(.select(4), .width(16)) multiplexer_2 (
    .in0(register_1_q), .in1(register_2_q), .in2(register_3_q), .in3(register_4_q), .in4(register_5_q),
    .in5(register_6_q), .in6(register_7_q), .in7(register_8_q), .in8(register_9_q), .in9(register_10_q),
    .in10(register_11_q), .in11(register_12_q), .in12(register_13_q), .in13(register_14_q),
    .in14(register_15_q), .in15(register_16_q), .out(Read_Value_2), .sel(Reading_Address_2), .en(Read_Enable));
endmodule
