// Logisim project Q1.circ as structural Verilog: 1 circuit, main circuit main
module main (
  input  [1:0] I0_I1,
  input  [1:0] I0_I1_2,
  input  [1:0] I0_I1_3,
  input  [1:0] I0_I1_4,
  output [1:0] Output,
  output [1:0] Output_2,
  output [1:0] Output_3,
  output [1:0] Output_4
);

  wire Bit_1_3_qn, Clock_2_out, Clock_3_out, Clock_4_out, Clock_out, d_ff_1_qn, d_ff_2_qn, multiplexer_5_out,
       multiplexer_6_out, multiplexer_7_out, multiplexer_8_out, xnor_1_out, xor_1_out;
  wire [0:0] Bit_1_qn, Bit_2__MSB_qn;
  wire [1:0] and_2_out, and_4_out, multiplexer_1_out, multiplexer_2_out, multiplexer_3_out, multiplexer_4_out;
  wire [1:1] Bit_1_2_qn;

  Clock Clock (.out(Clock_out));
  and and_1 (and_2_out[1], Bit_1_qn[0], Output_2[1]);
  and and_2 (and_2_out[0], Bit_2__MSB_qn[0], Bit_1_qn[0]);
  and and_3 (and_4_out[1], Output_2[1], Output_2[0]);
  and and_4 (and_4_out[0], Bit_2__MSB_qn[0], Output_2[0]);
  Multiplexer #(.select(2), .width(2), .enable("false")) multiplexer_1 (
    .in0(2'b00), .in1(and_4_out), .in2(and_2_out), .in3({Output_2[1], Bit_2__MSB_qn[0]}),
    .out(multiplexer_1_out), .sel(I0_I1_3));
  Multiplexer #(.select(2), .width(2), .enable("false")) multiplexer_2 (
    .in0(2'b00), .in1({Output_2[0], Bit_1_qn[0]}), .in2({Output_2[0], Bit_1_qn[0]}), .in3(2'b00),
    .out(multiplexer_2_out), .sel(I0_I1_3));
  S_R_Flip_Flop Bit_2__MSB (
    .S(multiplexer_1_out[0]), .clk(Clock_out), .R(multiplexer_1_out[1]), .Q(Output_2[1]),
    .Qn(Bit_2__MSB_qn[0]));  // open: preset, reset, en
  S_R_Flip_Flop Bit_1 (
    .S(multiplexer_2_out[0]), .clk(Clock_out), .R(multiplexer_2_out[1]), .Q(Output_2[0]), .Qn(Bit_1_qn[0]));  // open: preset, reset, en
  Clock Clock_2 (.out(Clock_2_out));
  Clock Clock_3 (.out(Clock_3_out));
  Multiplexer #(.select(2), .width(2), .enable("false")) multiplexer_3 (
    .in0(2'b00), .in1({2{Output[0]}}), .in2({2{Bit_1_2_qn[1]}}), .in3(2'b11), .out(multiplexer_3_out),
    .sel(I0_I1));
  Multiplexer #(.select(2), .width(2), .enable("false")) multiplexer_4 (
    .in0(2'b00), .in1(2'b11), .in2(2'b11), .in3(2'b00), .out(multiplexer_4_out), .sel(I0_I1));
  Multiplexer #(.select(2), .enable("false")) multiplexer_5 (
    .in0(1'b0), .in1(Output_4[0]), .in2(Bit_1_3_qn), .in3(1'b1), .out(multiplexer_5_out), .sel(I0_I1_4));
  Multiplexer #(.select(2), .enable("false")) multiplexer_6 (
    .in0(1'b0), .in1(1'b1), .in2(1'b1), .in3(1'b0), .out(multiplexer_6_out), .sel(I0_I1_4));
  J_K_Flip_Flop Bit_2__MSB_2 (
    .J(multiplexer_3_out[0]), .clk(Clock_2_out), .K(multiplexer_3_out[1]), .Q(Output[1]));  // open: Qn, preset, en, reset
  J_K_Flip_Flop Bit_1_2 (
    .J(multiplexer_4_out[0]), .clk(Clock_2_out), .K(multiplexer_4_out[1]), .Q(Output[0]), .Qn(Bit_1_2_qn[1]));  // open: preset, en, reset
  T_Flip_Flop Bit_2__MSB_3 (.clk(Clock_3_out), .T(multiplexer_5_out), .Q(Output_4[1]));  // open: Qn, preset, reset, en
  T_Flip_Flop Bit_1_3 (
    .clk(Clock_3_out), .T(multiplexer_6_out), .Q(Output_4[0]), .Qn(Bit_1_3_qn));  // open: preset, reset, en
  xnor xnor_1 (xnor_1_out, Output_3[0], Output_3[1]);
  xor xor_1 (xor_1_out, Output_3[0], Output_3[1]);
  Clock Clock_4 (.out(Clock_4_out));
  Multiplexer #(.select(2), .enable("false")) multiplexer_7 (
    .in0(Output_3[1]), .in1(xor_1_out), .in2(xnor_1_out), .in3(d_ff_1_qn), .out(multiplexer_7_out),
    .sel(I0_I1_2));
  Multiplexer #(.select(2), .enable("false")) multiplexer_8 (
    .in0(Output_3[0]), .in1(d_ff_2_qn), .in2(d_ff_2_qn), .in3(Output_3[0]), .out(multiplexer_8_out),
    .sel(I0_I1_2));
  D_Flip_Flop d_ff_1 (
    .clk(Clock_4_out), .D(multiplexer_7_out), .Q(Output_3[1]), .Qn(d_ff_1_qn));  // open: preset, en, reset
  D_Flip_Flop d_ff_2 (
    .clk(Clock_4_out), .D(multiplexer_8_out), .Q(Output_3[0]), .Qn(d_ff_2_qn));  // open: preset, en, reset

  // Notes on the sheet:
  //   1) Using SR Flip Flops
  //   2) Using JK Flip Flops
  //   3) Using T Flip Flops 
  //   2 Bit Multifunctional Counters
  //   4) Using D Flip Flops
  //   Bit 2 (MSB)
  //   Bit 1
endmodule
