// Logisim project Q1.circ as structural Verilog: 1 circuit, main circuit main
module main (
  input  [1:0] I0_I1,
  output [1:0] OUTPUT
);

  wire Clock_out;
  wire [1:0] multiplexer_1_out, multiplexer_2_out, multiplexer_3_out, multiplexer_4_out;

  Clock Clock (.out(Clock_out));
  Multiplexer #(.select(2), .width(2), .enable("false")) multiplexer_1 (
    .in0(2'b01), .in1(2'b10), .in2(2'b11), .in3(2'b00), .out(multiplexer_1_out), .sel(OUTPUT));
  Multiplexer #(.select(2), .width(2), .enable("false")) multiplexer_2 (
    .in0(2'b11), .in1(2'b00), .in2(2'b01), .in3(2'b10), .out(multiplexer_2_out), .sel(OUTPUT));
  Multiplexer #(.select(2), .width(2), .enable("false")) multiplexer_3 (
    .in0(2'b10), .in1(2'b11), .in2(2'b00), .in3(2'b01), .out(multiplexer_3_out), .sel(OUTPUT));
  Register #(.width(2)) _2_Bit_Register (.D(multiplexer_4_out), .Q(OUTPUT), .clk(Clock_out));  // open: en, clr
  Multiplexer #(.select(2), .width(2), .enable("false")) multiplexer_4 (
    .in0(OUTPUT), .in1(multiplexer_1_out), .in2(multiplexer_2_out), .in3(multiplexer_3_out),
    .out(multiplexer_4_out), .sel(I0_I1));

  // Notes on the sheet:
  //   Count up by 1
  //   Count Down by 1
  //   Count up by 2
  //   2 Bit Multipurpose Counter with MUX based FSM design
endmodule
