// Logisim project Q2.circ as structural Verilog: 5 circuits, main circuit main
module main (
  input  RESET,
  input  [15:0] in_2,
  input  [15:0] in_3,
  input  [15:0] in_4,
  input  [15:0] in_5,
  input  [15:0] in_6,
  input  [15:0] in_7,
  output out_8,
  output [31:0] out_9,
  output out_10,
  output [31:0] out_11
);

  wire clock_1_out, n32_bit_adder_1_carry;
  wire [15:0] register_1_q, register_2_q, register_3_q;
  wire [31:0] bit_extender_1_out, bit_extender_2_out, bit_extender_3_out, bit_extender_4_out,
       bit_extender_5_out, bit_extender_6_out, multiplier_1_out, multiplier_2_out, n32_bit_adder_1_out_3,
       register_4_q, register_5_q;

  Clock clock_1 (.out(clock_1_out));
  Register #(.width(16)) register_1 (.D(in_2), .Q(register_1_q), .clk(clock_1_out), .clr(RESET));  // open: en
  Register #(.width(16)) register_2 (.D(in_3), .Q(register_2_q), .clk(clock_1_out), .clr(RESET));  // open: en
  Register #(.width(16)) register_3 (.D(in_4), .Q(register_3_q), .clk(clock_1_out), .clr(RESET));  // open: en
  assign bit_extender_1_out = {{16{1'b0}}, register_1_q};  // Bit_Extender bit_extender_1
  assign bit_extender_2_out = {{16{1'b0}}, register_2_q};  // Bit_Extender bit_extender_2
  assign bit_extender_3_out = {{16{1'b0}}, register_3_q};  // Bit_Extender bit_extender_3
  assign bit_extender_4_out = {{16{1'b0}}, in_5};  // Bit_Extender bit_extender_4
  assign bit_extender_5_out = {{16{1'b0}}, in_6};  // Bit_Extender bit_extender_5
  assign bit_extender_6_out = {{16{1'b0}}, in_7};  // Bit_Extender bit_extender_6
  Multiplier #(.width(32)) multiplier_1 (
    .a(bit_extender_1_out), .b(bit_extender_2_out), .out(multiplier_1_out));  // open: cin, cout
  Register #(.width(32)) register_4 (
    .D(multiplier_1_out), .Q(register_4_q), .clk(clock_1_out), .clr(RESET));  // open: en
  Register #(.width(32)) register_5 (
    .D(bit_extender_3_out), .Q(register_5_q), .clk(clock_1_out), .clr(RESET));  // open: en
  Multiplier #(.width(32)) multiplier_2 (
    .a(bit_extender_4_out), .b(bit_extender_5_out), .out(multiplier_2_out));  // open: cin, cout
  _32_bit_Adder u_32_bit_adder_1 (
    .in_1(register_4_q), .in_2(register_5_q), .out_3(n32_bit_adder_1_out_3), .Carry(n32_bit_adder_1_carry));
  _32_bit_Adder u_32_bit_adder_2 (.in_1(multiplier_2_out), .in_2(bit_extender_6_out), .out_3(out_11), .Carry(out_10));
  Register #(.width(32)) register_6 (.D(n32_bit_adder_1_out_3), .Q(out_9), .clk(clock_1_out), .clr(RESET));  // open: en
  Register #(.width(1)) register_7 (.D(n32_bit_adder_1_carry), .Q(out_8), .clk(clock_1_out), .clr(RESET));  // open: en

  // Notes on the sheet:
  //   A
  //   B
  //   C
  //   CLK
  //   A
  //   B
  //   C
  //      multiplier
  //                              With pipeline register
  //                              Without pipeline register
  //      multiplier
  //        adder
  //        adder
  //   Y = A*B + C
  //   Y = A*B + C
endmodule

module Single_bit_Adder (
  input  C,
  input  A,
  input  B,
  output Sum,
  output Carry
);

  wire and_1_out, and_2_out, xor_1_out;

  xor xor_1 (xor_1_out, C, A);
  and and_1 (and_1_out, A, C);
  xor xor_2 (Sum, xor_1_out, B);
  and and_2 (and_2_out, B, xor_1_out);
  or or_1 (Carry, and_2_out, and_1_out);
endmodule

module _4_bit_Adder (
  input  C_in,
  input  A0,
  input  B0,
  input  A1,
  input  B1,
  input  A2,
  input  B2,
  input  A3,
  input  B3,
  output S0,
  output S1,
  output S2,
  output S3,
  output C_out
);

  wire single_bit_adder_1_carry, single_bit_adder_2_carry, single_bit_adder_3_carry;

  Single_bit_Adder single_bit_adder_1 (.C(C_in), .A(A0), .B(B0), .Sum(S0), .Carry(single_bit_adder_1_carry));
  Single_bit_Adder single_bit_adder_2 (
    .C(single_bit_adder_1_carry), .A(A1), .B(B1), .Sum(S1), .Carry(single_bit_adder_2_carry));
  Single_bit_Adder single_bit_adder_3 (
    .C(single_bit_adder_2_carry), .A(A2), .B(B2), .Sum(S2), .Carry(single_bit_adder_3_carry));
  Single_bit_Adder single_bit_adder_4 (.C(single_bit_adder_3_carry), .A(A3), .B(B3), .Sum(S3), .Carry(C_out));
endmodule

module _16_bit_Adder (
  input  in_1,
  input  [15:0] in_2,
  input  [15:0] in_3,
  output [15:0] out_4,
  output Carry
);

  wire n4_bit_adder_1_c_out, n4_bit_adder_2_c_out, n4_bit_adder_3_c_out, xor_1_out, xor_2_out, xor_3_out,
       xor_4_out, xor_5_out, xor_6_out, xor_7_out, xor_8_out, xor_9_out, xor_10_out, xor_11_out, xor_12_out,
       xor_13_out, xor_14_out, xor_15_out, xor_16_out;

  xor xor_1 (xor_1_out, in_1, in_3[0]);
  xor xor_2 (xor_2_out, in_1, in_3[1]);
  xor xor_3 (xor_3_out, in_1, in_3[2]);
  xor xor_4 (xor_4_out, in_1, in_3[3]);
  xor xor_5 (xor_5_out, in_1, in_3[4]);
  xor xor_6 (xor_6_out, in_1, in_3[5]);
  xor xor_7 (xor_7_out, in_1, in_3[6]);
  xor xor_8 (xor_8_out, in_1, in_3[7]);
  xor xor_9 (xor_9_out, in_1, in_3[8]);
  xor xor_10 (xor_10_out, in_1, in_3[9]);
  xor xor_11 (xor_11_out, in_1, in_3[10]);
  xor xor_12 (xor_12_out, in_1, in_3[11]);
  xor xor_13 (xor_13_out, in_1, in_3[12]);
  xor xor_14 (xor_14_out, in_1, in_3[13]);
  xor xor_15 (xor_15_out, in_1, in_3[14]);
  xor xor_16 (xor_16_out, in_1, in_3[15]);
  _4_bit_Adder u_4_bit_adder_1 (
    .C_in(in_1), .A0(in_2[0]), .B0(xor_1_out), .A1(in_2[1]), .B1(xor_2_out), .A2(in_2[2]), .B2(xor_3_out),
    .A3(in_2[3]), .B3(xor_4_out), .S0(out_4[0]), .S1(out_4[1]), .S2(out_4[2]), .S3(out_4[3]),
    .C_out(n4_bit_adder_1_c_out));
  _4_bit_Adder u_4_bit_adder_2 (
    .C_in(n4_bit_adder_1_c_out), .A0(in_2[4]), .B0(xor_5_out), .A1(in_2[5]), .B1(xor_6_out), .A2(in_2[6]),
    .B2(xor_7_out), .A3(in_2[7]), .B3(xor_8_out), .S0(out_4[4]), .S1(out_4[5]), .S2(out_4[6]), .S3(out_4[7]),
    .C_out(n4_bit_adder_2_c_out));
  _4_bit_Adder u_4_bit_adder_3 (
    .C_in(n4_bit_adder_2_c_out), .A0(in_2[8]), .B0(xor_9_out), .A1(in_2[9]), .B1(xor_10_out), .A2(in_2[10]),
    .B2(xor_11_out), .A3(in_2[11]), .B3(xor_12_out), .S0(out_4[8]), .S1(out_4[9]), .S2(out_4[10]),
    .S3(out_4[11]), .C_out(n4_bit_adder_3_c_out));
  _4_bit_Adder u_4_bit_adder_4 (
    .C_in(n4_bit_adder_3_c_out), .A0(in_2[12]), .B0(xor_13_out), .A1(in_2[13]), .B1(xor_14_out),
    .A2(in_2[14]), .B2(xor_15_out), .A3(in_2[15]), .B3(xor_16_out), .S0(out_4[12]), .S1(out_4[13]),
    .S2(out_4[14]), .S3(out_4[15]), .C_out(Carry));

  // Other names for the same wires on the sheet: A0 = in_2[0]; A1 = in_2[1]; A2 = in_2[2]; A3 = in_2[3]; A4 = in_2[4];
  //   A5 = in_2[5]; A6 = in_2[6]; A7 = in_2[7]; A8 = in_2[8]; A9 = in_2[9]; A10 = in_2[10]; A11 = in_2[11];
  //   A12 = in_2[12]; A13 = in_2[13]; A14 = in_2[14]; A15 = in_2[15]; B0 = in_3[0]; B1 = in_3[1]; B2 = in_3[2];
  //   B3 = in_3[3]; B4 = in_3[4]; B5 = in_3[5]; B6 = in_3[6]; B7 = in_3[7]; B8 = in_3[8]; B9 = in_3[9];
  //   B10 = in_3[10]; B11 = in_3[11]; B12 = in_3[12]; B13 = in_3[13]; B14 = in_3[14]; B15 = in_3[15]

  // Notes on the sheet:
  //   A
  //   B
  //             Output
endmodule

module _32_bit_Adder (
  input  [31:0] in_1,
  input  [31:0] in_2,
  output [31:0] out_3,
  output Carry
);

  wire n16_bit_adder_1_carry;

  _16_bit_Adder u_16_bit_adder_1 (
    .in_2(in_1[15:0]), .in_3(in_2[15:0]), .in_1(1'b0), .out_4(out_3[15:0]), .Carry(n16_bit_adder_1_carry));
  _16_bit_Adder u_16_bit_adder_2 (
    .in_2(in_1[31:16]), .in_3(in_2[31:16]), .in_1(n16_bit_adder_1_carry), .out_4(out_3[31:16]), .Carry(Carry));

  // Notes on the sheet:
  //   A
  //   B
endmodule
