// Logisim project Q3.circ as structural Verilog: 1 circuit, main circuit main
module main (
  input  Input,
  input  Clear,
  output Output
);

  wire Clock_out;
  wire [3:0] shift_register_1_q0;

  Clock Clock (.out(Clock_out));
  Shift_Register #(.length(4)) shift_register_1 (
    .shift(1'b1), .in(Input), .clk(Clock_out), .clr(Clear), .q0(shift_register_1_q0[0]),
    .q1(shift_register_1_q0[1]), .q2(shift_register_1_q0[2]), .q3(shift_register_1_q0[3]));  // open: out, load, d0, d1, d2, d3
  Multiplexer #(.select(4), .enable("false")) multiplexer_1 (
    .in0(1'b0), .in1(1'b0), .in2(1'b0), .in3(1'b0), .in4(1'b1), .in5(1'b0), .in6(1'b0), .in7(1'b0),
    .in8(1'b0), .in9(1'b1), .in10(1'b0), .in11(1'b1), .in12(1'b0), .in13(1'b0), .in14(1'b0), .in15(1'b0),
    .out(Output), .sel(shift_register_1_q0));

  // Notes on the sheet:
  //   Shift Register stores the 4 previous input values
  //   0100, 1001, 1011 Sequence Detector
  //   And supplies corresponding 4-Bit number as control input to the MUX
endmodule
