// Logisim project 1901CS75_A2.circ as structural Verilog: 1 circuit, main circuit main
module main (
  input  X,
  output Y
);

  wire and_1_out, and_2_out, and_3_out, Clk_out, not_1_out, or_1_out, or_2_out, t_ff_1_q, t_ff_2_q, xor_1_out;

  Clock Clk (.out(Clk_out));
  not not_1 (not_1_out, X);
  and and_1 (and_1_out, not_1_out, t_ff_2_q);
  and and_2 (and_2_out, X, t_ff_1_q);
  xor xor_1 (xor_1_out, t_ff_2_q, X);
  and and_3 (and_3_out, not_1_out, t_ff_1_q);
  or or_1 (or_1_out, and_1_out, and_2_out);
  or or_2 (or_2_out, xor_1_out, and_3_out);
  T_Flip_Flop t_ff_1 (.clk(Clk_out), .T(or_1_out), .Q(t_ff_1_q));  // open: Qn, preset, reset, en
  T_Flip_Flop t_ff_2 (.clk(Clk_out), .T(or_2_out), .Q(t_ff_2_q));  // open: Qn, preset, reset, en
  and and_4 (Y, X, t_ff_1_q, t_ff_2_q);
endmodule
