// Logisim project 1901CS75_A3.circ as structural Verilog: 2 circuits, main circuit main
module main (
  input  J,
  input  K,
  output Q,
  output Q_prime
);

  wire Clk_out, nand_1_out, nand_2_out, nand_3_out, nand_4_out, nand_5_out, nand_6_out, not_1_out;

  Clock Clk (.out(Clk_out));
  nand nand_1 (nand_1_out, Q_prime, J, Clk_out);
  nand nand_2 (nand_2_out, Clk_out, K, Q);
  not not_1 (not_1_out, Clk_out);
  nand nand_3 (nand_3_out, nand_1_out, nand_4_out);
  nand nand_4 (nand_4_out, nand_3_out, nand_2_out);
  nand nand_5 (nand_5_out, nand_3_out, not_1_out);
  nand nand_6 (nand_6_out, not_1_out, nand_4_out);
  nand nand_7 (Q, nand_5_out, Q_prime);
  nand nand_8 (Q_prime, Q, nand_6_out);

  // Notes on the sheet:
  //   Master-Slave JK Flip Flop
endmodule

module Level_Sensitive_JK_Flip_Flop (
  input  J,
  input  K,
  output Q,
  output Q_prime
);

  wire Clk_out, nand_1_out, nand_2_out;

  Clock Clk (.out(Clk_out));
  nand nand_1 (nand_1_out, Q_prime, J, Clk_out);
  nand nand_2 (nand_2_out, Clk_out, K, Q);
  nand nand_3 (Q, nand_1_out, Q_prime);
  nand nand_4 (Q_prime, Q, nand_2_out);

  // Notes on the sheet:
  //   Level Sensitive JK Flip Flop
endmodule
